// Digital circuit ALU.dig as structural Verilog
module ALU (
  input  [4:0] Ctrl,
  input  [31:0] s1,
  input  [31:0] s2,
  output zero,
  output [31:0] result
);

  wire comparator_1_eq, comparator_1_gt, comparator_2_eq, comparator_2_gt, not_1_out, or_2_out, or_3_out;
  wire [0:0] comparator_1_lt, comparator_2_lt;
  wire [31:0] add_1_s, and_1_out, barrelshifter_1_out, barrelshifter_2_out, barrelshifter_3_out, div_1_q,
       div_1_r, div_2_q, div_2_r, multiplexer_1_out, multiplexer_2_out, multiplexer_3_out, multiplexer_4_out,
       or_1_out, sub_1_s, xor_1_out;
  wire [63:0] mul_1_mul, mul_2_mul;

  Add #(.Bits(32)) add_1 (.a(s1), .b(s2), .c_i(1'b0), .s(add_1_s));  // open: c_o
  Sub #(.Bits(32)) sub_1 (.a(s1), .b(s2), .c_i(1'b0), .s(sub_1_s));  // open: c_o
  BarrelShifter #(.Bits(32)) barrelshifter_1 (.in(s1), .shift(s2[5:0]), .out(barrelshifter_1_out));
  assign xor_1_out = s1 ^ s2;  // XOr xor_1, 32 bits wide
  BarrelShifter #(.Bits(32), .direction("right")) barrelshifter_2 (.in(s1), .shift(s2[5:0]), .out(barrelshifter_2_out));
  BarrelShifter #(.Bits(32), .barrelShifterMode("arithmetic"), .direction("right")) barrelshifter_3 (
    .in(s1), .shift(s2[5:0]), .out(barrelshifter_3_out));
  assign or_1_out = s1 | s2;  // Or or_1, 32 bits wide
  assign and_1_out = s1 & s2;  // And and_1, 32 bits wide
  Mul #(.Bits(32)) mul_1 (.a(s1), .b(s2), .mul(mul_1_mul));
  Mul #(.Signed("true"), .Bits(32)) mul_2 (.a(s1), .b(s2), .mul(mul_2_mul));
  Div #(.Bits(32), .Signed("true")) div_1 (.a(s1), .b(s2), .q(div_1_q), .r(div_1_r));
  Div #(.Bits(32)) div_2 (.a(s1), .b(s2), .q(div_2_q), .r(div_2_r));
  Comparator #(.Signed("true"), .Bits(32)) comparator_1 (
    .a(s1), .b(s2), .gt(comparator_1_gt), .eq(comparator_1_eq), .lt(comparator_1_lt[0]));
  Comparator #(.Bits(32)) comparator_2 (
    .a(s1), .b(s2), .gt(comparator_2_gt), .eq(comparator_2_eq), .lt(comparator_2_lt[0]));
  Multiplexer #(.Bits(32)) multiplexer_1 (.sel(Ctrl[3]), .in_0(add_1_s), .in_1(sub_1_s), .out(multiplexer_1_out));
  Multiplexer #(.Bits(32)) multiplexer_2 (
    .sel(Ctrl[3]), .in_0(barrelshifter_2_out), .in_1(barrelshifter_3_out), .out(multiplexer_2_out));
  or or_2 (or_2_out, comparator_1_eq, comparator_1_gt);
  or or_3 (or_3_out, comparator_2_gt, comparator_2_eq);
  Multiplexer #(.Selector_Bits(3), .Bits(32)) multiplexer_3 (
    .sel(Ctrl[2:0]), .in_0(multiplexer_1_out), .in_1(barrelshifter_1_out),
    .in_2({{31{1'b0}}, comparator_1_lt[0]}), .in_3({{31{1'b0}}, comparator_2_lt[0]}), .in_4(xor_1_out),
    .in_5(multiplexer_2_out), .in_6(or_1_out), .in_7(and_1_out), .out(multiplexer_3_out));
  Multiplexer #(.Bits(32), .Selector_Bits(3)) multiplexer_4 (
    .sel(Ctrl[2:0]), .in_0(mul_1_mul[31:0]), .in_1(mul_2_mul[63:32]), .in_2(mul_2_mul[31:0]),
    .in_3(mul_1_mul[63:32]), .in_4(div_1_q), .in_5(div_2_q), .in_6(div_1_r), .in_7(div_2_r),
    .out(multiplexer_4_out));
  not not_1 (not_1_out, comparator_1_eq);
  Multiplexer #(.Bits(32)) multiplexer_5 (
    .sel(Ctrl[4]), .in_0(multiplexer_3_out), .in_1(multiplexer_4_out), .out(result));
  Multiplexer #(.Selector_Bits(3)) multiplexer_6 (
    .sel(Ctrl[2:0]), .in_0(comparator_1_eq), .in_1(not_1_out), .in_2(1'b0), .in_3(1'b0),
    .in_4(comparator_1_lt[0]), .in_5(or_2_out), .in_6(comparator_2_lt[0]), .in_7(or_3_out), .out(zero));

  // Other names for the same wires on the sheet: funct3[2:0] = Ctrl[2:0]; funct7 = Ctrl[3]
endmodule
