// Digital circuit AddressDecorder.dig as structural Verilog
module AddressDecorder (
  input  [31:0] A,
  input  [31:0] WD,
  input  [31:0] Imm,
  input  [2:0] funct3,
  input  [31:0] bD,
  input  MemWrite,
  output GPUen,
  output [23:0] A_share,
  output [31:0] D,
  output GCen,
  output RAMen
);

  wire en_0, en_1, en_2, en_3;
  wire [7:0] multiplexer_1_out, multiplexer_2_out, multiplexer_3_out, multiplexer_4_out;
  wire [15:0] multiplexer_5_out, multiplexer_6_out;
  wire [31:0] multiplexer_7_out;

  Decoder #(.Selector_Bits(2)) decoder_1 (.sel(Imm[1:0]), .out_0(en_0), .out_1(en_1), .out_2(en_2), .out_3(en_3));
  Multiplexer #(.Bits(8)) multiplexer_1 (.sel(en_3), .in_0(bD[31:24]), .in_1(WD[7:0]), .out(multiplexer_1_out));
  Multiplexer #(.Bits(8)) multiplexer_2 (.sel(en_2), .in_0(bD[23:16]), .in_1(WD[7:0]), .out(multiplexer_2_out));
  Multiplexer #(.Bits(8)) multiplexer_3 (.sel(en_1), .in_0(bD[15:8]), .in_1(WD[7:0]), .out(multiplexer_3_out));
  Multiplexer #(.Bits(8)) multiplexer_4 (.sel(en_0), .in_0(bD[7:0]), .in_1(WD[7:0]), .out(multiplexer_4_out));
  Multiplexer #(.Bits(16)) multiplexer_5 (.sel(en_0), .in_0(bD[15:0]), .in_1(WD[15:0]), .out(multiplexer_5_out));
  Multiplexer #(.Bits(16)) multiplexer_6 (.sel(en_1), .in_0(bD[31:16]), .in_1(WD[15:0]), .out(multiplexer_6_out));
  Multiplexer #(.Selector_Bits(3), .Bits(32)) multiplexer_7 (
    .sel(funct3), .in_0({multiplexer_1_out, multiplexer_2_out, multiplexer_3_out, multiplexer_4_out}),
    .in_1({multiplexer_6_out, multiplexer_5_out}), .in_2(WD), .in_3({32{1'b0}}), .in_4({32{1'b0}}),
    .in_5({32{1'b0}}), .in_6({32{1'b0}}), .in_7({32{1'b0}}), .out(multiplexer_7_out));
  Multiplexer #(.Bits(32)) multiplexer_8 (.sel(MemWrite), .in_0({32{1'b0}}), .in_1(multiplexer_7_out), .out(D));
  and and_1 (RAMen, ~A[24], ~A[25], ~A[26], ~A[27], ~A[28], ~A[29], ~A[30], ~A[31]);  // And
  and and_2 (GPUen, ~A[24], A[25], ~A[26], ~A[27], ~A[28], ~A[29], ~A[30], ~A[31]);  // And
  and and_3 (GCen, A[24], ~A[25], ~A[26], ~A[27], ~A[28], ~A[29], ~A[30], ~A[31]);  // And

  assign A_share = A[23:0];

  // Other names for the same wires on the sheet: share[23:0] = A[23:0]; Adec_0 = A[24]; Adec_1 = A[25];
  //   Adec_2 = A[26]; Adec_3 = A[27]; Adec_4 = A[28]; Adec_5 = A[29]; Adec_6 = A[30]; Adec_7 = A[31];
  //   D_0[7:0] = bD[7:0]; D_1[7:0] = bD[15:8]; D_2[7:0] = bD[23:16]; D_3[7:0] = bD[31:24]; Imm_t[1:0] = Imm[1:0]
endmodule
