// Digital circuit Byte_RAM.dig as structural Verilog
module Byte_RAM (
  input  en,
  input  WE,
  input  C,
  input  [1:0] mode,
  input  [23:0] A_1,
  input  [31:0] Din,
  input  [23:0] A_2,
  output [31:0] D_1,
  output [31:0] D_2
);

  wire b, h, or_1_out, or_2_out, w, WE_0, WE_1, WE_2;
  wire [23:0] RA_1, RA_2, RA_3, WA_1, WA_2, WA_3;

  Add #(.Bits(24)) add_1 (.a(A_1), .b(24'h1), .c_i(1'b0), .s(WA_1));  // open: c_o
  Add #(.Bits(24)) add_2 (.a(A_1), .b(24'h2), .c_i(1'b0), .s(WA_2));  // open: c_o
  Add #(.Bits(24)) add_3 (.a(A_1), .b(24'h3), .c_i(1'b0), .s(WA_3));  // open: c_o
  Add #(.Bits(24)) add_4 (.a(A_2), .b(24'h1), .c_i(1'b0), .s(RA_1));  // open: c_o
  Add #(.Bits(24)) add_5 (.a(A_2), .b(24'h2), .c_i(1'b0), .s(RA_2));  // open: c_o
  Add #(.Bits(24)) add_6 (.a(A_2), .b(24'h3), .c_i(1'b0), .s(RA_3));  // open: c_o
  // MultiPortRAM #(.readPorts(8), .AddrBits(24), .writePorts(4), .Bits(8)) multiportram_1: pin names not known; wires that end beside it: WE_0, A_1, Din[7:0], WE_1, WA_1, Din[15:8], WE_2, WA_2, Din[23:16], WE_2, WA_3, Din[31:24], A_1, WA_1, WA_2, WA_3, A_2, RA_1, RA_2, RA_3, C, D_1[7:0], D_1[15:8], D_1[23:16], D_1[31:24], D_2[7:0], D_2[15:8], D_2[23:16], D_2[31:24]
  and and_1 (b, ~mode[0], ~mode[1]);  // And
  and and_2 (h, mode[0], ~mode[1]);  // And
  and and_3 (w, ~mode[0], mode[1]);  // And
  or or_1 (or_1_out, b, h, w);
  or or_2 (or_2_out, h, w);
  and and_4 (WE_0, en, WE, or_1_out);
  and and_5 (WE_1, en, WE, or_2_out);
  and and_6 (WE_2, en, WE, w);

  // Other names for the same wires on the sheet: RA_0[23:0] = A_2; WA_0[23:0] = A_1; WE_3 = WE_2
endmodule
