// Digital circuit DMUX_8bit.dig as structural Verilog
module DMUX_8bit (
  input  [4:0] sel,
  input  [7:0] in,
  output [7:0] o_0,
  output [7:0] o_1,
  output [7:0] o_2,
  output [7:0] o_3,
  output [7:0] o_4,
  output [7:0] o_5,
  output [7:0] o_6,
  output [7:0] o_7,
  output [7:0] o_8,
  output [7:0] o_9,
  output [7:0] o_10,
  output [7:0] o_11,
  output [7:0] o_12,
  output [7:0] o_13,
  output [7:0] o_14,
  output [7:0] o_15,
  output [7:0] o_16,
  output [7:0] o_17,
  output [7:0] o_18,
  output [7:0] o_19,
  output [7:0] o_20,
  output [7:0] o_21,
  output [7:0] o_22,
  output [7:0] o_23,
  output [7:0] o_24,
  output [7:0] o_25,
  output [7:0] o_26,
  output [7:0] o_27,
  output [7:0] o_28,
  output [7:0] o_29,
  output [7:0] o_30,
  output [7:0] o_31
);

  wire and_1_out, and_2_out, and_3_out, and_4_out, and_5_out, and_6_out, and_7_out, and_8_out, and_9_out,
       and_10_out, and_11_out, and_12_out, and_13_out, and_14_out, and_15_out, and_16_out, and_17_out,
       and_18_out, and_19_out, and_20_out, and_21_out, and_22_out, and_23_out, and_24_out, and_25_out,
       and_26_out, and_27_out, and_28_out, and_29_out, and_30_out, and_31_out, and_32_out;

  and and_1 (and_1_out, ~sel[4], ~sel[3], ~sel[2], ~sel[1], ~sel[0]);  // And
  and and_2 (and_2_out, ~sel[4], ~sel[3], ~sel[2], ~sel[1], sel[0]);  // And
  and and_3 (and_3_out, ~sel[4], ~sel[3], ~sel[2], sel[1], ~sel[0]);  // And
  and and_4 (and_4_out, ~sel[4], ~sel[3], ~sel[2], sel[1], sel[0]);  // And
  and and_5 (and_5_out, ~sel[4], ~sel[3], sel[2], ~sel[1], ~sel[0]);  // And
  and and_6 (and_6_out, ~sel[4], ~sel[3], sel[2], ~sel[1], sel[0]);  // And
  and and_7 (and_7_out, ~sel[4], ~sel[3], sel[2], sel[1], ~sel[0]);  // And
  and and_8 (and_8_out, ~sel[4], ~sel[3], sel[2], sel[1], sel[0]);  // And
  and and_9 (and_9_out, ~sel[4], sel[3], ~sel[2], ~sel[1], ~sel[0]);  // And
  and and_10 (and_10_out, ~sel[4], sel[3], ~sel[2], ~sel[1], sel[0]);  // And
  and and_11 (and_11_out, ~sel[4], sel[3], ~sel[2], sel[1], ~sel[0]);  // And
  and and_12 (and_12_out, ~sel[4], sel[3], ~sel[2], sel[1], sel[0]);  // And
  and and_13 (and_13_out, ~sel[4], sel[3], sel[2], ~sel[1], ~sel[0]);  // And
  and and_14 (and_14_out, ~sel[4], sel[3], sel[2], ~sel[1], sel[0]);  // And
  and and_15 (and_15_out, ~sel[4], sel[3], sel[2], sel[1], ~sel[0]);  // And
  and and_16 (and_16_out, ~sel[4], sel[3], sel[2], sel[1], sel[0]);  // And
  and and_17 (and_17_out, sel[4], ~sel[3], ~sel[2], ~sel[1], ~sel[0]);  // And
  and and_18 (and_18_out, sel[4], ~sel[3], ~sel[2], ~sel[1], sel[0]);  // And
  and and_19 (and_19_out, sel[4], ~sel[3], ~sel[2], sel[1], ~sel[0]);  // And
  and and_20 (and_20_out, sel[4], ~sel[3], ~sel[2], sel[1], sel[0]);  // And
  and and_21 (and_21_out, sel[4], ~sel[3], sel[2], ~sel[1], ~sel[0]);  // And
  and and_22 (and_22_out, sel[4], ~sel[3], sel[2], ~sel[1], sel[0]);  // And
  and and_23 (and_23_out, sel[4], ~sel[3], sel[2], sel[1], ~sel[0]);  // And
  and and_24 (and_24_out, sel[4], ~sel[3], sel[2], sel[1], sel[0]);  // And
  and and_25 (and_25_out, sel[4], sel[3], ~sel[2], ~sel[1], ~sel[0]);  // And
  and and_26 (and_26_out, sel[4], sel[3], ~sel[2], ~sel[1], sel[0]);  // And
  and and_27 (and_27_out, sel[4], sel[3], ~sel[2], sel[1], ~sel[0]);  // And
  and and_28 (and_28_out, sel[4], sel[3], ~sel[2], sel[1], sel[0]);  // And
  and and_29 (and_29_out, sel[4], sel[3], sel[2], ~sel[1], ~sel[0]);  // And
  and and_30 (and_30_out, sel[4], sel[3], sel[2], ~sel[1], sel[0]);  // And
  and and_31 (and_31_out, sel[4], sel[3], sel[2], sel[1], ~sel[0]);  // And
  and and_32 (and_32_out, sel[4], sel[3], sel[2], sel[1], sel[0]);
  assign o_0 = and_1_out ? in : 8'bz;  // Driver driver_1
  assign o_1 = and_2_out ? in : 8'bz;  // Driver driver_2
  assign o_2 = and_3_out ? in : 8'bz;  // Driver driver_3
  assign o_3 = and_4_out ? in : 8'bz;  // Driver driver_4
  assign o_4 = and_5_out ? in : 8'bz;  // Driver driver_5
  assign o_5 = and_6_out ? in : 8'bz;  // Driver driver_6
  assign o_6 = and_7_out ? in : 8'bz;  // Driver driver_7
  assign o_7 = and_8_out ? in : 8'bz;  // Driver driver_8
  assign o_8 = and_9_out ? in : 8'bz;  // Driver driver_9
  assign o_9 = and_10_out ? in : 8'bz;  // Driver driver_10
  assign o_10 = and_11_out ? in : 8'bz;  // Driver driver_11
  assign o_11 = and_12_out ? in : 8'bz;  // Driver driver_12
  assign o_12 = and_13_out ? in : 8'bz;  // Driver driver_13
  assign o_13 = and_14_out ? in : 8'bz;  // Driver driver_14
  assign o_14 = and_15_out ? in : 8'bz;  // Driver driver_15
  assign o_15 = and_16_out ? in : 8'bz;  // Driver driver_16
  assign o_16 = and_17_out ? in : 8'bz;  // Driver driver_17
  assign o_17 = and_18_out ? in : 8'bz;  // Driver driver_18
  assign o_18 = and_19_out ? in : 8'bz;  // Driver driver_19
  assign o_19 = and_20_out ? in : 8'bz;  // Driver driver_20
  assign o_20 = and_21_out ? in : 8'bz;  // Driver driver_21
  assign o_21 = and_22_out ? in : 8'bz;  // Driver driver_22
  assign o_22 = and_23_out ? in : 8'bz;  // Driver driver_23
  assign o_23 = and_24_out ? in : 8'bz;  // Driver driver_24
  assign o_24 = and_25_out ? in : 8'bz;  // Driver driver_25
  assign o_25 = and_26_out ? in : 8'bz;  // Driver driver_26
  assign o_26 = and_27_out ? in : 8'bz;  // Driver driver_27
  assign o_27 = and_28_out ? in : 8'bz;  // Driver driver_28
  assign o_28 = and_29_out ? in : 8'bz;  // Driver driver_29
  assign o_29 = and_30_out ? in : 8'bz;  // Driver driver_30
  assign o_30 = and_31_out ? in : 8'bz;  // Driver driver_31
  assign o_31 = and_32_out ? in : 8'bz;  // Driver driver_32
endmodule
