// Digital circuit DMUX_exe.dig as structural Verilog
module DMUX_exe (
  input  [2:0] sel,
  input  in,
  output o_0,
  output o_1,
  output o_2,
  output o_3,
  output o_4,
  output o_5,
  output o_6,
  output o_7
);

  wire and_1_out, and_2_out, and_3_out, and_4_out, and_5_out, and_6_out, and_7_out, and_8_out;

  and and_1 (and_1_out, ~sel[2], ~sel[1], ~sel[0]);  // And
  and and_2 (and_2_out, ~sel[2], ~sel[1], sel[0]);  // And
  and and_3 (and_3_out, ~sel[2], sel[1], ~sel[0]);  // And
  and and_4 (and_4_out, ~sel[2], sel[1], sel[0]);  // And
  and and_5 (and_5_out, sel[2], ~sel[1], ~sel[0]);  // And
  and and_6 (and_6_out, sel[2], ~sel[1], sel[0]);  // And
  and and_7 (and_7_out, sel[2], sel[1], ~sel[0]);  // And
  and and_8 (and_8_out, sel[2], sel[1], sel[0]);
  assign o_0 = and_1_out ? in : 1'bz;  // Driver driver_1
  assign o_1 = and_2_out ? in : 1'bz;  // Driver driver_2
  assign o_2 = and_3_out ? in : 1'bz;  // Driver driver_3
  assign o_3 = and_4_out ? in : 1'bz;  // Driver driver_4
  assign o_4 = and_5_out ? in : 1'bz;  // Driver driver_5
  assign o_5 = and_6_out ? in : 1'bz;  // Driver driver_6
  assign o_6 = and_7_out ? in : 1'bz;  // Driver driver_7
  assign o_7 = and_8_out ? in : 1'bz;  // Driver driver_8
endmodule
