// Digital circuit DivisionPrototype.dig as structural Verilog
module DivisionPrototype (
  input  [7:0] DD,
  input  [7:0] DS,
  input  C,
  input  [7:0] DD_2,
  input  [7:0] DS_2,
  output [7:0] out_4,
  output [7:0] out_5
);

  wire comparator_1_eq, comparator_1_gt, comparator_2_eq, comparator_2_gt, comparator_3_eq, comparator_3_gt,
       comparator_4_eq, comparator_4_gt, comparator_5_eq, comparator_5_gt, comparator_6_eq, comparator_6_gt,
       comparator_7_eq, comparator_7_gt, comparator_8_eq, comparator_8_gt, undriven, undriven_2;
  wire [2:0] priorityencoder_1_num;
  wire [7:0] multiplexer_2_out, multiplexer_3_out, multiplexer_4_out, multiplexer_5_out, multiplexer_6_out,
       multiplexer_7_out, multiplexer_8_out, sub_1_s, sub_2_s, sub_3_s, sub_4_s, sub_5_s, sub_6_s, sub_7_s,
       sub_8_s;
  wire [14:0] barrelshifter_1_out, multiplexer_1_out;

  PriorityEncoder #(.Selector_Bits(3)) priorityencoder_1 (
    .in0(DS_2[0]), .in1(DS_2[1]), .in2(DS_2[2]), .in3(DS_2[3]), .in4(DS_2[4]), .in5(DS_2[5]), .in6(DS_2[6]),
    .in7(DS_2[7]), .num(priorityencoder_1_num));  // open: any
  BarrelShifter #(.Bits(15)) barrelshifter_1 (
    .in({{7{1'b0}}, DD_2}), .shift(priorityencoder_1_num), .out(barrelshifter_1_out));
  Multiplexer #(.Bits(15)) multiplexer_1 (.in_0(barrelshifter_1_out), .out(multiplexer_1_out));  // open: sel, in_1
  Comparator #(.Bits(8)) comparator_1 (
    .a({{7{1'b0}}, DD[7]}), .b(DS), .gt(comparator_1_gt), .eq(comparator_1_eq));  // open: lt
  Sub #(.Bits(8)) sub_1 (.a({{7{1'b0}}, DD[7]}), .b(DS), .c_i(1'b0), .s(sub_1_s));  // open: c_o
  or or_1 (out_5[7], comparator_1_gt, comparator_1_eq);
  Register #(.Bits(8)) PR (.D(multiplexer_1_out[7:0]), .C(undriven), .en(undriven_2));  // open: Q
  Multiplexer #(.Bits(8)) multiplexer_2 (
    .sel(out_5[7]), .in_0({{7{1'b0}}, DD[7]}), .in_1(sub_1_s), .out(multiplexer_2_out));
  Comparator #(.Bits(8)) comparator_2 (
    .a({multiplexer_2_out[6:0], DD[6]}), .b(DS), .gt(comparator_2_gt), .eq(comparator_2_eq));  // open: lt
  Sub #(.Bits(8)) sub_2 (.a({multiplexer_2_out[6:0], DD[6]}), .b(DS), .c_i(1'b0), .s(sub_2_s));  // open: c_o
  or or_2 (out_5[6], comparator_2_gt, comparator_2_eq);
  Multiplexer #(.Bits(8)) multiplexer_3 (
    .sel(out_5[6]), .in_0({multiplexer_2_out[6:0], DD[6]}), .in_1(sub_2_s), .out(multiplexer_3_out));
  Comparator #(.Bits(8)) comparator_3 (
    .a({multiplexer_3_out[6:0], DD[5]}), .b(DS), .gt(comparator_3_gt), .eq(comparator_3_eq));  // open: lt
  Sub #(.Bits(8)) sub_3 (.a({multiplexer_3_out[6:0], DD[5]}), .b(DS), .c_i(1'b0), .s(sub_3_s));  // open: c_o
  or or_3 (out_5[5], comparator_3_gt, comparator_3_eq);
  Multiplexer #(.Bits(8)) multiplexer_4 (
    .sel(out_5[5]), .in_0({multiplexer_3_out[6:0], DD[5]}), .in_1(sub_3_s), .out(multiplexer_4_out));
  Comparator #(.Bits(8)) comparator_4 (
    .a({multiplexer_4_out[6:0], DD[4]}), .b(DS), .gt(comparator_4_gt), .eq(comparator_4_eq));  // open: lt
  Sub #(.Bits(8)) sub_4 (.a({multiplexer_4_out[6:0], DD[4]}), .b(DS), .c_i(1'b0), .s(sub_4_s));  // open: c_o
  or or_4 (out_5[4], comparator_4_gt, comparator_4_eq);
  Multiplexer #(.Bits(8)) multiplexer_5 (
    .sel(out_5[4]), .in_0({multiplexer_4_out[6:0], DD[4]}), .in_1(sub_4_s), .out(multiplexer_5_out));
  Comparator #(.Bits(8)) comparator_5 (
    .a({multiplexer_5_out[6:0], DD[3]}), .b(DS), .gt(comparator_5_gt), .eq(comparator_5_eq));  // open: lt
  Sub #(.Bits(8)) sub_5 (.a({multiplexer_5_out[6:0], DD[3]}), .b(DS), .c_i(1'b0), .s(sub_5_s));  // open: c_o
  or or_5 (out_5[3], comparator_5_gt, comparator_5_eq);
  Multiplexer #(.Bits(8)) multiplexer_6 (
    .sel(out_5[3]), .in_0({multiplexer_5_out[6:0], DD[3]}), .in_1(sub_5_s), .out(multiplexer_6_out));
  Comparator #(.Bits(8)) comparator_6 (
    .a({multiplexer_6_out[6:0], DD[2]}), .b(DS), .gt(comparator_6_gt), .eq(comparator_6_eq));  // open: lt
  Sub #(.Bits(8)) sub_6 (.a({multiplexer_6_out[6:0], DD[2]}), .b(DS), .c_i(1'b0), .s(sub_6_s));  // open: c_o
  or or_6 (out_5[2], comparator_6_gt, comparator_6_eq);
  Multiplexer #(.Bits(8)) multiplexer_7 (
    .sel(out_5[2]), .in_0({multiplexer_6_out[6:0], DD[2]}), .in_1(sub_6_s), .out(multiplexer_7_out));
  Comparator #(.Bits(8)) comparator_7 (
    .a({multiplexer_7_out[6:0], DD[1]}), .b(DS), .gt(comparator_7_gt), .eq(comparator_7_eq));  // open: lt
  Sub #(.Bits(8)) sub_7 (.a({multiplexer_7_out[6:0], DD[1]}), .b(DS), .c_i(1'b0), .s(sub_7_s));  // open: c_o
  or or_7 (out_5[1], comparator_7_gt, comparator_7_eq);
  Multiplexer #(.Bits(8)) multiplexer_8 (
    .sel(out_5[1]), .in_0({multiplexer_7_out[6:0], DD[1]}), .in_1(sub_7_s), .out(multiplexer_8_out));
  Comparator #(.Bits(8)) comparator_8 (
    .a({multiplexer_8_out[6:0], DD[0]}), .b(DS), .gt(comparator_8_gt), .eq(comparator_8_eq));  // open: lt
  Sub #(.Bits(8)) sub_8 (.a({multiplexer_8_out[6:0], DD[0]}), .b(DS), .c_i(1'b0), .s(sub_8_s));  // open: c_o
  or or_8 (out_5[0], comparator_8_gt, comparator_8_eq);
  Multiplexer #(.Bits(8)) multiplexer_9 (
    .sel(out_5[0]), .in_0({multiplexer_8_out[6:0], DD[0]}), .in_1(sub_8_s), .out(out_4));
  // Pins of 8 and 15 bits meet at multiplexer_1_out

  // Other names for the same wires on the sheet: dd_0 = DD[0]; dd_1 = DD[1]; dd_2_t = DD[2]; dd_3 = DD[3];
  //   dd_4 = DD[4]; dd_5 = DD[5]; dd_6 = DD[6]; q_0 = out_5[0]; q_1 = out_5[1]; q_2 = out_5[2]; q_3 = out_5[3];
  //   q_4 = out_5[4]; q_5 = out_5[5]; q_6 = out_5[6]; q_7 = out_5[7]
endmodule
