// Digital circuit Extender.dig as structural Verilog
module Extender (
  input  [2:0] src,
  input  [24:0] Imm,
  output [31:0] Extended
);

  wire [11:0] multiplexer_1_out;
  wire [31:0] bitextender_1_out, multiplexer_2_out;

  BitExtender #(.inputBits(20), .outputBits(32)) bitextender_1 (.in(Imm[24:5]), .out(bitextender_1_out));
  Multiplexer #(.Bits(12)) multiplexer_1 (
    .sel(src[0]), .in_0(Imm[24:13]), .in_1({Imm[24:18], Imm[4:0]}), .out(multiplexer_1_out));
  Multiplexer #(.Bits(32)) multiplexer_2 (
    .sel(src[0]), .in_0(bitextender_1_out), .in_1({Imm[24:5], {12{1'b0}}}), .out(multiplexer_2_out));
  Multiplexer #(.Selector_Bits(2), .Bits(32)) multiplexer_3 (
    .sel(src[2:1]), .in_0({{21{multiplexer_1_out[11]}}, multiplexer_1_out[10:0]}), .in_1(multiplexer_2_out),
    .in_2({{20{1'b0}}, Imm[24:13]}), .in_3({{20{1'b0}}, Imm[24:13]}), .out(Extended));

  // Notes on the sheet:
  //   I-fmt (imm)
  //   S-fmt (imm)
  //   U,J-fmt (imm)
  //   U,J-fmt (upimm)
endmodule
