// Digital circuit FPU.dig as structural Verilog
module FPU (
  input  [4:0] Ctrl,
  input  [31:0] s1,
  input  [31:0] s2,
  output [31:0] result
);

  wire floatcomparator_1_eq, floatcomparator_1_lt, or_1_out;
  wire [0:0] multiplexer_2_out;
  wire [31:0] float2int_1_int, float2uint_1_uint, floatadder_1_s, floatdivision_1_q, floatmax_1_max,
       floatmin_1_min, floatmultiply_1_mul, floatsubtract_1_s, int2float_1_f, multiplexer_1_out,
       multiplexer_3_out, multiplexer_4_out, uint2float_1_uf;

  FloatAdder floatadder_1 (.L(s1), .R(s2), .S(floatadder_1_s));
  FloatSubtract floatsubtract_1 (.L(s1), .R(s2), .S(floatsubtract_1_s));
  FloatMultiply floatmultiply_1 (.L(s1), .R(s2), .mul(floatmultiply_1_mul));
  FloatDivision floatdivision_1 (.L(s1), .R(s2), .q(floatdivision_1_q));
  FloatMin floatmin_1 (.L(s1), .R(s2), .Min(floatmin_1_min));
  FloatMax floatmax_1 (.L(s1), .R(s2), .Max(floatmax_1_max));
  FloatComparator floatcomparator_1 (.L(s1), .R(s2), .eq(floatcomparator_1_eq), .lt(floatcomparator_1_lt));  // open: gt
  Float2int float2int_1 (.L(s1), .\int (float2int_1_int));
  Float2uInt float2uint_1 (.L(s1), .uint(float2uint_1_uint));
  int2float int2float_1 (.L(s1), .f(int2float_1_f));
  uint2float uint2float_1 (.L(s1), .uf(uint2float_1_uf));
  Multiplexer #(.Selector_Bits(3), .Bits(32)) multiplexer_1 (
    .sel(Ctrl[2:0]), .in_0(floatadder_1_s), .in_1(floatsubtract_1_s), .in_2(floatmultiply_1_mul),
    .in_3(floatdivision_1_q), .in_4(floatmin_1_min), .in_5(floatmax_1_max), .in_6({32{1'b0}}),
    .in_7({32{1'b0}}), .out(multiplexer_1_out));
  Multiplexer #(.Selector_Bits(2)) multiplexer_2 (
    .sel(Ctrl[1:0]), .in_0(floatcomparator_1_eq), .in_1(floatcomparator_1_lt), .in_2(or_1_out), .in_3(1'b0),
    .out(multiplexer_2_out[0]));
  or or_1 (or_1_out, floatcomparator_1_eq, floatcomparator_1_lt);
  Multiplexer #(.Selector_Bits(2), .Bits(32)) multiplexer_3 (
    .sel(Ctrl[1:0]), .in_0(float2int_1_int), .in_1(float2uint_1_uint), .in_2(s1), .in_3({32{1'b0}}),
    .out(multiplexer_3_out));
  Multiplexer #(.Selector_Bits(2), .Bits(32)) multiplexer_4 (
    .sel(Ctrl[1:0]), .in_0(int2float_1_f), .in_1(uint2float_1_uf), .in_2(s1), .in_3({32{1'b0}}),
    .out(multiplexer_4_out));
  Multiplexer #(.Selector_Bits(2), .Bits(32)) multiplexer_5 (
    .sel(Ctrl[4:3]), .in_0(multiplexer_1_out), .in_1({{31{1'b0}}, multiplexer_2_out[0]}),
    .in_2(multiplexer_3_out), .in_3(multiplexer_4_out), .out(result));
  // Pins of 4 and 5 bits meet at Ctrl
endmodule
