// Digital circuit Float2int.dig as structural Verilog
module Float2int (
  input  [31:0] L,
  output [31:0] \int 
);

  wire and_1_out, comparator_1_lt, or_2_out, or_3_out;
  wire [8:0] sub_1_s;
  wire [23:23] or_1_out;
  wire [30:0] add_1_s, multiplexer_2_out;
  wire [31:0] add_2_s, not_1_out;
  wire [53:0] barrelshifter_1_out, multiplexer_1_out;

  or or_1 (or_1_out[23], L[30], L[29], L[28], L[27], L[26], L[25], L[24], L[23]);
  Sub #(.Bits(9)) sub_1 (.a({1'b0, L[30:23]}), .b(9'h7f), .c_i(1'b0), .s(sub_1_s));  // open: c_o
  BarrelShifter #(.Bits(54), .barrelSigned("true")) barrelshifter_1 (
    .in({{30{1'b0}}, or_1_out[23], L[22:0]}), .shift(sub_1_s[6:0]), .out(barrelshifter_1_out));
  Comparator #(.Signed("true"), .Bits(9)) comparator_1 (
    .a(sub_1_s), .b({9{1'b1}}), .lt(comparator_1_lt));  // open: gt, eq
  Multiplexer #(.Bits(54)) multiplexer_1 (
    .sel(comparator_1_lt), .in_0(barrelshifter_1_out), .in_1({54{1'b0}}), .out(multiplexer_1_out));
  or or_2 (or_2_out, multiplexer_1_out[20], multiplexer_1_out[19], multiplexer_1_out[18], multiplexer_1_out[17], multiplexer_1_out[16], multiplexer_1_out[15], multiplexer_1_out[14], multiplexer_1_out[13], multiplexer_1_out[12], multiplexer_1_out[11], multiplexer_1_out[10], multiplexer_1_out[9], multiplexer_1_out[8], multiplexer_1_out[7], multiplexer_1_out[6], multiplexer_1_out[5], multiplexer_1_out[4], multiplexer_1_out[3], multiplexer_1_out[2], multiplexer_1_out[1], multiplexer_1_out[0]);
  or or_3 (or_3_out, or_2_out, multiplexer_1_out[21], multiplexer_1_out[23]);
  and and_1 (and_1_out, or_3_out, multiplexer_1_out[22]);
  Add #(.Bits(31)) add_1 (.a(multiplexer_1_out[53:23]), .b({31{1'b0}}), .c_i(1'b1), .s(add_1_s));  // open: c_o
  Multiplexer #(.Bits(31)) multiplexer_2 (
    .sel(and_1_out), .in_0(multiplexer_1_out[53:23]), .in_1(add_1_s), .out(multiplexer_2_out));
  assign not_1_out = ~{1'b0, multiplexer_2_out};  // Not not_1, 32 bits wide
  Add #(.Bits(32)) add_2 (.a(not_1_out), .b({32{1'b0}}), .c_i(1'b1), .s(add_2_s));  // open: c_o
  Multiplexer #(.Bits(32)) multiplexer_3 (.sel(L[31]), .in_0({1'b0, multiplexer_2_out}), .in_1(add_2_s), .out(\int ));
endmodule
