// Digital circuit Float2uInt.dig as structural Verilog
module Float2uInt (
  input  [31:0] L,
  output [31:0] uint
);

  wire and_1_out, comparator_1_lt, or_2_out, or_3_out;
  wire [8:0] sub_1_s;
  wire [20:0] multiplexer_1_out;
  wire [22:21] multiplexer_1_out_2;
  wire [23:23] or_1_out;
  wire [31:0] add_1_s, multiplexer_1_out_3;
  wire [54:0] barrelshifter_1_out;

  or or_1 (or_1_out[23], L[30], L[29], L[28], L[27], L[26], L[25], L[24], L[23]);
  Sub #(.Bits(9)) sub_1 (.a({1'b0, L[30:23]}), .b(9'h7f), .c_i(1'b0), .s(sub_1_s));  // open: c_o
  BarrelShifter #(.Bits(55), .barrelSigned("true")) barrelshifter_1 (
    .in({{31{1'b0}}, or_1_out[23], L[22:0]}), .shift(sub_1_s[6:0]), .out(barrelshifter_1_out));
  Comparator #(.Signed("true"), .Bits(9)) comparator_1 (
    .a(sub_1_s), .b({9{1'b1}}), .lt(comparator_1_lt));  // open: gt, eq
  Multiplexer #(.Bits(55)) multiplexer_1 (
    .sel(comparator_1_lt), .in_0(barrelshifter_1_out), .in_1({55{1'b0}}),
    .out({multiplexer_1_out_3, multiplexer_1_out_2, multiplexer_1_out}));
  or or_2 (or_2_out, multiplexer_1_out[20], multiplexer_1_out[19], multiplexer_1_out[18], multiplexer_1_out[17], multiplexer_1_out[16], multiplexer_1_out[15], multiplexer_1_out[14], multiplexer_1_out[13], multiplexer_1_out[12], multiplexer_1_out[11], multiplexer_1_out[10], multiplexer_1_out[9], multiplexer_1_out[8], multiplexer_1_out[7], multiplexer_1_out[6], multiplexer_1_out[5], multiplexer_1_out[4], multiplexer_1_out[3], multiplexer_1_out[2], multiplexer_1_out[1], multiplexer_1_out[0]);
  or or_3 (or_3_out, or_2_out, multiplexer_1_out_2[21], multiplexer_1_out_3[0]);
  and and_1 (and_1_out, or_3_out, multiplexer_1_out_2[22]);
  Add #(.Bits(32)) add_1 (.a(multiplexer_1_out_3), .b({32{1'b0}}), .c_i(1'b1), .s(add_1_s));  // open: c_o
  Multiplexer #(.Bits(32)) multiplexer_2 (.sel(and_1_out), .in_0(multiplexer_1_out_3), .in_1(add_1_s), .out(uint));
endmodule
