// Digital circuit FloatComparator.dig as structural Verilog
module FloatComparator (
  input  [31:0] L,
  input  [31:0] R,
  output gt,
  output eq,
  output lt
);

  wire comparator_1_eq, comparator_1_gt, comparator_1_lt, comparator_2_gt, comparator_2_lt, xnor_1_out;
  wire [2:0] and_1_out, comparator_2_eq, multiplexer_1_out, multiplexer_5_out;

  xnor xnor_1 (xnor_1_out, L[31], R[31]);
  and and_1 (and_1_out[0], ~L[31], R[31]);  // And
  and and_2 (and_1_out[2], L[31], ~R[31]);  // And
  Comparator #(.Bits(8)) comparator_1 (
    .a(L[30:23]), .b(R[30:23]), .gt(comparator_1_gt), .eq(comparator_1_eq), .lt(comparator_1_lt));
  Comparator #(.Bits(23)) comparator_2 (
    .a(L[22:0]), .b(R[22:0]), .gt(comparator_2_gt), .eq(comparator_2_eq[1]), .lt(comparator_2_lt));
  Multiplexer multiplexer_1 (.sel(R[31]), .in_0(comparator_1_gt), .in_1(comparator_1_lt), .out(multiplexer_1_out[0]));
  Multiplexer multiplexer_2 (.sel(R[31]), .in_0(comparator_1_lt), .in_1(comparator_1_gt), .out(multiplexer_1_out[2]));
  Multiplexer multiplexer_3 (.sel(R[31]), .in_0(comparator_2_gt), .in_1(comparator_2_lt), .out(comparator_2_eq[0]));
  Multiplexer multiplexer_4 (.sel(R[31]), .in_0(comparator_2_lt), .in_1(comparator_2_gt), .out(comparator_2_eq[2]));
  Multiplexer #(.Bits(3)) multiplexer_5 (
    .sel(comparator_1_eq), .in_0({multiplexer_1_out[2], 1'b0, multiplexer_1_out[0]}), .in_1(comparator_2_eq),
    .out(multiplexer_5_out));
  Multiplexer #(.Bits(3)) multiplexer_6 (
    .sel(xnor_1_out), .in_0({and_1_out[2], 1'b0, and_1_out[0]}), .in_1(multiplexer_5_out), .out({lt, eq, gt}));
endmodule
