// Digital circuit FloatMax.dig as structural Verilog
module FloatMax (
  input  [31:0] L,
  input  [31:0] R,
  output [31:0] Max
);

  wire and_1_out, comparator_1_eq, comparator_1_gt, comparator_1_lt, comparator_2_gt, comparator_2_lt,
       multiplexer_4_out, multiplexer_5_out, nand_1_out, xnor_1_out;
  wire [31:0] multiplexer_1_out, multiplexer_2_out, multiplexer_3_out, multiplexer_6_out;

  and and_1 (and_1_out, L[31], ~R[31]);  // And
  nand nand_1 (nand_1_out, L[31], R[31]);
  xnor xnor_1 (xnor_1_out, L[31], R[31]);
  Multiplexer #(.Bits(32)) multiplexer_1 (.sel(and_1_out), .in_0(L), .in_1(R), .out(multiplexer_1_out));
  Multiplexer #(.Bits(32)) multiplexer_2 (.sel(multiplexer_4_out), .in_0(L), .in_1(R), .out(multiplexer_2_out));
  Multiplexer #(.Bits(32)) multiplexer_3 (.sel(multiplexer_5_out), .in_0(L), .in_1(R), .out(multiplexer_3_out));
  Comparator #(.Bits(8)) comparator_1 (
    .a(L[30:23]), .b(R[30:23]), .gt(comparator_1_gt), .eq(comparator_1_eq), .lt(comparator_1_lt));
  Multiplexer multiplexer_4 (.sel(nand_1_out), .in_0(comparator_1_gt), .in_1(comparator_1_lt), .out(multiplexer_4_out));
  Comparator #(.Bits(23)) comparator_2 (
    .a(L[22:0]), .b(R[22:0]), .gt(comparator_2_gt), .lt(comparator_2_lt));  // open: eq
  Multiplexer multiplexer_5 (.sel(nand_1_out), .in_0(comparator_2_gt), .in_1(comparator_2_lt), .out(multiplexer_5_out));
  Multiplexer #(.Bits(32)) multiplexer_6 (
    .sel(comparator_1_eq), .in_0(multiplexer_2_out), .in_1(multiplexer_3_out), .out(multiplexer_6_out));
  Multiplexer #(.Bits(32)) multiplexer_7 (
    .sel(xnor_1_out), .in_0(multiplexer_1_out), .in_1(multiplexer_6_out), .out(Max));
endmodule
