// Digital circuit FloatMultiply.dig as structural Verilog
module FloatMultiply (
  input  [31:0] L,
  input  [31:0] R,
  output [31:0] mul
);

  wire and_1_out, and_2_out, and_3_out, and_4_out, exzero, Infinity, nor_1_out, not_1_out, or_4_out,
       or_5_out, or_6_out;
  wire [4:0] priorityencoder_1_num;
  wire [5:0] sub_2_s;
  wire [7:0] bitextender_1_out, ex, multiplexer_2_out, sub_3_s;
  wire [8:0] add_1_s;
  wire [8:8] sub_1_s;
  wire [22:0] mul_1_mul;
  wire [23:23] or_1_out, or_2_out;
  wire [26:0] add_2_s, barrelshifter_1_out, mul_1_mul_2, multiplexer_1_out;

  or or_1 (or_1_out[23], L[30], L[29], L[28], L[27], L[26], L[25], L[24], L[23]);
  or or_2 (or_2_out[23], R[30], R[29], R[28], R[27], R[26], R[25], R[24], R[23]);
  Add #(.Bits(9)) add_1 (.a({1'b0, L[30:23]}), .b({1'b0, R[30:23]}), .c_i(1'b0), .s(add_1_s));  // open: c_o
  // Probe on {1'b0, or_1_out[23], L[22:0]}
  // Probe on {1'b0, or_2_out[23], R[22:0]}
  and and_1 (and_1_out, L[23], L[24], L[25], L[26], L[27], L[28], L[29], L[30]);
  and and_2 (and_2_out, R[23], R[24], R[25], R[26], R[27], R[28], R[29], R[30]);
  Mul #(.Bits(25)) mul_1 (
    .a({1'b0, or_1_out[23], L[22:0]}), .b({1'b0, or_2_out[23], R[22:0]}), .mul({mul_1_mul_2, mul_1_mul}));
  Sub #(.Bits(9)) sub_1 (.a(add_1_s), .b(9'h7f), .c_i(1'b0), .s({sub_1_s[8], ex}), .c_o(exzero));
  not not_1 (not_1_out, exzero);
  // Probe on mul_1_mul_2
  xor xor_1 (mul[31], L[31], R[31]);
  and and_3 (and_3_out, sub_1_s[8], not_1_out);
  // Probe on ex
  or or_3 (Infinity, and_3_out, and_1_out, and_2_out);
  or or_4 (or_4_out, mul_1_mul[20], mul_1_mul[19], mul_1_mul[18], mul_1_mul[17], mul_1_mul[16], mul_1_mul[15], mul_1_mul[14], mul_1_mul[13], mul_1_mul[12], mul_1_mul[11], mul_1_mul[10], mul_1_mul[9], mul_1_mul[8], mul_1_mul[7], mul_1_mul[6], mul_1_mul[5], mul_1_mul[4], mul_1_mul[3], mul_1_mul[2], mul_1_mul[1], mul_1_mul[0]);
  or or_5 (or_5_out, or_4_out, mul_1_mul[21], mul_1_mul_2[0]);
  and and_4 (and_4_out, or_5_out, mul_1_mul[22]);
  Add #(.Bits(27)) add_2 (.a(mul_1_mul_2), .b({27{1'b0}}), .c_i(1'b1), .s(add_2_s));  // open: c_o
  Multiplexer #(.Bits(27)) multiplexer_1 (.sel(and_4_out), .in_0(mul_1_mul_2), .in_1(add_2_s), .out(multiplexer_1_out));
  PriorityEncoder #(.Selector_Bits(5)) priorityencoder_1 (
    .in0(multiplexer_1_out[0]), .in1(multiplexer_1_out[1]), .in2(multiplexer_1_out[2]),
    .in3(multiplexer_1_out[3]), .in4(multiplexer_1_out[4]), .in5(multiplexer_1_out[5]),
    .in6(multiplexer_1_out[6]), .in7(multiplexer_1_out[7]), .in8(multiplexer_1_out[8]),
    .in9(multiplexer_1_out[9]), .in10(multiplexer_1_out[10]), .in11(multiplexer_1_out[11]),
    .in12(multiplexer_1_out[12]), .in13(multiplexer_1_out[13]), .in14(multiplexer_1_out[14]),
    .in15(multiplexer_1_out[15]), .in16(multiplexer_1_out[16]), .in17(multiplexer_1_out[17]),
    .in18(multiplexer_1_out[18]), .in19(multiplexer_1_out[19]), .in20(multiplexer_1_out[20]),
    .in21(multiplexer_1_out[21]), .in22(multiplexer_1_out[22]), .in23(multiplexer_1_out[23]),
    .in24(multiplexer_1_out[24]), .in25(multiplexer_1_out[25]), .in26(multiplexer_1_out[26]), .in27(1'b0),
    .in28(1'b0), .in29(1'b0), .in30(1'b0), .in31(1'b0), .num(priorityencoder_1_num));  // open: any
  BarrelShifter #(.Bits(27), .barrelSigned("true")) barrelshifter_1 (
    .in(multiplexer_1_out), .shift(sub_2_s), .out(barrelshifter_1_out));
  Sub #(.Bits(6)) sub_2 (.a(6'b010111), .b({1'b0, priorityencoder_1_num}), .c_i(1'b0), .s(sub_2_s));  // open: c_o
  nor nor_1 (nor_1_out, multiplexer_1_out[26], multiplexer_1_out[25], multiplexer_1_out[24], multiplexer_1_out[23], multiplexer_1_out[22], multiplexer_1_out[21], multiplexer_1_out[20], multiplexer_1_out[19], multiplexer_1_out[18], multiplexer_1_out[17], multiplexer_1_out[16], multiplexer_1_out[15], multiplexer_1_out[14], multiplexer_1_out[13], multiplexer_1_out[12], multiplexer_1_out[11], multiplexer_1_out[10], multiplexer_1_out[9], multiplexer_1_out[8], multiplexer_1_out[7], multiplexer_1_out[6], multiplexer_1_out[5], multiplexer_1_out[4], multiplexer_1_out[3], multiplexer_1_out[2], multiplexer_1_out[1], multiplexer_1_out[0]);
  BitExtender #(.inputBits(6), .outputBits(8)) bitextender_1 (.in(sub_2_s), .out(bitextender_1_out));
  // Probe on bitextender_1_out
  Sub #(.Bits(8)) sub_3 (.a(ex), .b(bitextender_1_out), .c_i(1'b0), .s(sub_3_s));  // open: c_o
  or or_6 (or_6_out, nor_1_out, exzero);
  Multiplexer #(.Bits(8)) multiplexer_2 (.sel(or_6_out), .in_0(sub_3_s), .in_1({8{1'b0}}), .out(multiplexer_2_out));
  Multiplexer #(.Bits(23)) multiplexer_3 (
    .sel(Infinity), .in_0(barrelshifter_1_out[22:0]), .in_1({23{1'b0}}), .out(mul[22:0]));
  Multiplexer #(.Bits(8)) multiplexer_4 (.sel(Infinity), .in_0(multiplexer_2_out), .in_1({8{1'b1}}), .out(mul[30:23]));

  // Other names for the same wires on the sheet: sign = mul[31]
endmodule
