// Digital circuit FloatREG_FILE.dig as structural Verilog
module FloatREG_FILE (
  input  WE,
  input  [31:0] WD,
  input  [4:0] A_fs1,
  input  [4:0] A_fs2,
  input  [4:0] A_fd,
  input  C,
  output [31:0] fs1,
  output [31:0] fs2,
  output [31:0] Q_10,
  output [31:0] Q_11,
  output [31:0] Q_12,
  output [31:0] Q_13
);

  wire en_0, en_1, en_2, en_3, en_4, en_5, en_6, en_7, en_8, en_9, en_10, en_11, en_12, en_13, en_14, en_15,
       en_16, en_17, en_18, en_19, en_20, en_21, en_22, en_23, en_24, en_25, en_26, en_27, en_28, en_29,
       en_30, en_31;
  wire [31:0] Q_0, Q_1, Q_2, Q_3, Q_4, Q_5, Q_6, Q_7, Q_8, Q_9, Q_14, Q_15, Q_16, Q_17, Q_18, Q_19, Q_20,
       Q_21, Q_22, Q_23, Q_24, Q_25, Q_26, Q_27, Q_28, Q_29, Q_30, Q_31;

  Demultiplexer #(.Selector_Bits(5)) demultiplexer_1 (
    .sel(A_fd), .in(WE), .out_0(en_0), .out_1(en_1), .out_2(en_2), .out_3(en_3), .out_4(en_4), .out_5(en_5),
    .out_6(en_6), .out_7(en_7), .out_8(en_8), .out_9(en_9), .out_10(en_10), .out_11(en_11), .out_12(en_12),
    .out_13(en_13), .out_14(en_14), .out_15(en_15), .out_16(en_16), .out_17(en_17), .out_18(en_18),
    .out_19(en_19), .out_20(en_20), .out_21(en_21), .out_22(en_22), .out_23(en_23), .out_24(en_24),
    .out_25(en_25), .out_26(en_26), .out_27(en_27), .out_28(en_28), .out_29(en_29), .out_30(en_30),
    .out_31(en_31));
  Register #(.Bits(32)) register_1 (.D(WD), .C(C), .en(en_0), .Q(Q_0));
  Register #(.Bits(32)) register_2 (.D(WD), .C(C), .en(en_5), .Q(Q_5));
  Register #(.Bits(32)) register_3 (.D(WD), .C(C), .en(en_10), .Q(Q_10));
  Register #(.Bits(32)) register_4 (.D(WD), .C(C), .en(en_15), .Q(Q_15));
  Register #(.Bits(32)) register_5 (.D(WD), .C(C), .en(en_20), .Q(Q_20));
  Register #(.Bits(32)) register_6 (.D(WD), .C(C), .en(en_25), .Q(Q_25));
  Register #(.Bits(32)) register_7 (.D(WD), .C(C), .en(en_30), .Q(Q_30));
  Register #(.Bits(32)) register_8 (.D(WD), .C(C), .en(en_1), .Q(Q_1));
  Register #(.Bits(32)) register_9 (.D(WD), .C(C), .en(en_6), .Q(Q_6));
  Register #(.Bits(32)) register_10 (.D(WD), .C(C), .en(en_11), .Q(Q_11));
  Register #(.Bits(32)) register_11 (.D(WD), .C(C), .en(en_16), .Q(Q_16));
  Register #(.Bits(32)) register_12 (.D(WD), .C(C), .en(en_21), .Q(Q_21));
  Register #(.Bits(32)) register_13 (.D(WD), .C(C), .en(en_26), .Q(Q_26));
  Register #(.Bits(32)) register_14 (.D(WD), .C(C), .en(en_31), .Q(Q_31));
  Register #(.Bits(32)) register_15 (.D(WD), .C(C), .en(en_2), .Q(Q_2));
  Register #(.Bits(32)) register_16 (.D(WD), .C(C), .en(en_7), .Q(Q_7));
  Register #(.Bits(32)) register_17 (.D(WD), .C(C), .en(en_12), .Q(Q_12));
  Register #(.Bits(32)) register_18 (.D(WD), .C(C), .en(en_17), .Q(Q_17));
  Register #(.Bits(32)) register_19 (.D(WD), .C(C), .en(en_22), .Q(Q_22));
  Register #(.Bits(32)) register_20 (.D(WD), .C(C), .en(en_27), .Q(Q_27));
  Register #(.Bits(32)) register_21 (.D(WD), .C(C), .en(en_3), .Q(Q_3));
  Register #(.Bits(32)) register_22 (.D(WD), .C(C), .en(en_8), .Q(Q_8));
  Register #(.Bits(32)) register_23 (.D(WD), .C(C), .en(en_13), .Q(Q_13));
  Register #(.Bits(32)) register_24 (.D(WD), .C(C), .en(en_18), .Q(Q_18));
  Register #(.Bits(32)) register_25 (.D(WD), .C(C), .en(en_23), .Q(Q_23));
  Register #(.Bits(32)) register_26 (.D(WD), .C(C), .en(en_28), .Q(Q_28));
  Register #(.Bits(32)) register_27 (.D(WD), .C(C), .en(en_4), .Q(Q_4));
  Register #(.Bits(32)) register_28 (.D(WD), .C(C), .en(en_9), .Q(Q_9));
  Register #(.Bits(32)) register_29 (.D(WD), .C(C), .en(en_14), .Q(Q_14));
  Register #(.Bits(32)) register_30 (.D(WD), .C(C), .en(en_19), .Q(Q_19));
  Register #(.Bits(32)) register_31 (.D(WD), .C(C), .en(en_24), .Q(Q_24));
  Register #(.Bits(32)) register_32 (.D(WD), .C(C), .en(en_29), .Q(Q_29));
  Multiplexer #(.Selector_Bits(5), .Bits(32)) multiplexer_1 (
    .sel(A_fs1), .in_0(Q_0), .in_1(Q_1), .in_2(Q_2), .in_3(Q_3), .in_4(Q_4), .in_5(Q_5), .in_6(Q_6),
    .in_7(Q_7), .in_8(Q_8), .in_9(Q_9), .in_10(Q_10), .in_11(Q_11), .in_12(Q_12), .in_13(Q_13), .in_14(Q_14),
    .in_15(Q_15), .in_16(Q_16), .in_17(Q_17), .in_18(Q_18), .in_19(Q_19), .in_20(Q_20), .in_21(Q_21),
    .in_22(Q_22), .in_23(Q_23), .in_24(Q_24), .in_25(Q_25), .in_26(Q_26), .in_27(Q_27), .in_28(Q_28),
    .in_29(Q_29), .in_30(Q_30), .in_31(Q_31), .out(fs1));
  Multiplexer #(.Selector_Bits(5), .Bits(32)) multiplexer_2 (
    .sel(A_fs2), .in_0(Q_0), .in_1(Q_1), .in_2(Q_2), .in_3(Q_3), .in_4(Q_4), .in_5(Q_5), .in_6(Q_6),
    .in_7(Q_7), .in_8(Q_8), .in_9(Q_9), .in_10(Q_10), .in_11(Q_11), .in_12(Q_12), .in_13(Q_13), .in_14(Q_14),
    .in_15(Q_15), .in_16(Q_16), .in_17(Q_17), .in_18(Q_18), .in_19(Q_19), .in_20(Q_20), .in_21(Q_21),
    .in_22(Q_22), .in_23(Q_23), .in_24(Q_24), .in_25(Q_25), .in_26(Q_26), .in_27(Q_27), .in_28(Q_28),
    .in_29(Q_29), .in_30(Q_30), .in_31(Q_31), .out(fs2));
  // Pins of 1 and 32 bits meet at Q_10
  // Pins of 1 and 32 bits meet at Q_11
  // Pins of 1 and 32 bits meet at Q_12
  // Pins of 1 and 32 bits meet at Q_13
endmodule
