// Digital circuit FloatSubtract.dig as structural Verilog
module FloatSubtract (
  input  [31:0] L,
  input  [31:0] R,
  output [31:0] S
);

  wire and_1_out, and_2_out, and_3_out, and_4_out, and_5_out, comparator_1_lt, NaN_A, NaN_B, nor_1_out,
       nor_2_out, nor_3_out, or_6_out, or_7_out;
  wire [4:0] priorityencoder_1_num;
  wire [5:0] sub_3_s;
  wire [7:0] bitextender_1_out, larger, multiplexer_4_out, multiplexer_13_out, sub_1_s, sub_4_s;
  wire [21:0] barrelshifter_1_out;
  wire [23:23] or_2_out, or_3_out;
  wire [24:0] add_4_s, barrelshifter_2_out, multiplexer_12_out;
  wire [26:0] add_1_s, add_2_s, multiplexer_7_out, multiplexer_8_out, not_1_out, not_2_out, or_5_out;
  wire [26:3] multiplexer_1_out;
  wire [27:0] add_3_s, multiplexer_11_out, not_3_out, sub_2_s;
  wire [28:0] multiplexer_9_out, multiplexer_10_out;
  wire [28:28] multiplexer_5_out, multiplexer_6_out;
  wire [47:24] multiplexer_2_out;

  or or_1 (NaN_A, L[0], L[1], L[2], L[3], L[4], L[5], L[6], L[7], L[8], L[9], L[10], L[11], L[12], L[13], L[14], L[15], L[16], L[17], L[18], L[19], L[20], L[21], L[22]);
  or or_2 (or_2_out[23], L[30], L[29], L[28], L[27], L[26], L[25], L[24], L[23]);
  or or_3 (or_3_out[23], R[30], R[29], R[28], R[27], R[26], R[25], R[24], R[23]);
  or or_4 (NaN_B, R[0], R[1], R[2], R[3], R[4], R[5], R[6], R[7], R[8], R[9], R[10], R[11], R[12], R[13], R[14], R[15], R[16], R[17], R[18], R[19], R[20], R[21], R[22]);
  Multiplexer #(.Bits(24)) multiplexer_1 (
    .sel(comparator_1_lt), .in_0({or_2_out[23], L[22:0]}), .in_1({or_3_out[23], R[22:0]}),
    .out(multiplexer_1_out));
  Multiplexer #(.Bits(24)) multiplexer_2 (
    .sel(comparator_1_lt), .in_0({or_3_out[23], R[22:0]}), .in_1({or_2_out[23], L[22:0]}),
    .out(multiplexer_2_out));
  Multiplexer #(.Bits(8)) multiplexer_3 (.sel(comparator_1_lt), .in_0(L[30:23]), .in_1(R[30:23]), .out(larger));
  Multiplexer #(.Bits(8)) multiplexer_4 (
    .sel(comparator_1_lt), .in_0(R[30:23]), .in_1(L[30:23]), .out(multiplexer_4_out));
  Multiplexer multiplexer_5 (.sel(comparator_1_lt), .in_0(L[31]), .in_1(R[31]), .out(multiplexer_5_out[28]));
  Multiplexer multiplexer_6 (.sel(comparator_1_lt), .in_0(R[31]), .in_1(L[31]), .out(multiplexer_6_out[28]));
  Comparator #(.Bits(8)) comparator_1 (.a(L[30:23]), .b(R[30:23]), .lt(comparator_1_lt));  // open: gt, eq
  BarrelShifter #(.Bits(48), .direction("right")) barrelshifter_1 (
    .in({multiplexer_2_out, {24{1'b0}}}), .shift(sub_1_s[5:0]), .out({or_5_out[26:1], barrelshifter_1_out}));
  Sub #(.Bits(8)) sub_1 (.a(larger), .b(multiplexer_4_out), .c_i(1'b0), .s(sub_1_s));  // open: c_o
  or or_5 (or_5_out[0], barrelshifter_1_out[21], barrelshifter_1_out[20], barrelshifter_1_out[19], barrelshifter_1_out[18], barrelshifter_1_out[17], barrelshifter_1_out[16], barrelshifter_1_out[15], barrelshifter_1_out[14], barrelshifter_1_out[13], barrelshifter_1_out[12], barrelshifter_1_out[11], barrelshifter_1_out[10], barrelshifter_1_out[9], barrelshifter_1_out[8], barrelshifter_1_out[7], barrelshifter_1_out[6], barrelshifter_1_out[5], barrelshifter_1_out[4], barrelshifter_1_out[3], barrelshifter_1_out[2], barrelshifter_1_out[1], barrelshifter_1_out[0]);
  assign not_1_out = ~{multiplexer_1_out, 3'b000};  // Not not_1, 27 bits wide
  Add #(.Bits(27)) add_1 (.a(not_1_out), .b({27{1'b0}}), .c_i(1'b1), .s(add_1_s));  // open: c_o
  assign not_2_out = ~or_5_out;  // Not not_2, 27 bits wide
  Add #(.Bits(27)) add_2 (.a(not_2_out), .b({27{1'b0}}), .c_i(1'b1), .s(add_2_s));  // open: c_o
  Multiplexer #(.Bits(27)) multiplexer_7 (
    .sel(multiplexer_5_out[28]), .in_0({multiplexer_1_out, 3'b000}), .in_1(add_1_s), .out(multiplexer_7_out));
  Multiplexer #(.Bits(27)) multiplexer_8 (
    .sel(multiplexer_6_out[28]), .in_0(or_5_out), .in_1(add_2_s), .out(multiplexer_8_out));
  Multiplexer #(.Bits(29)) multiplexer_9 (
    .sel(comparator_1_lt), .in_0({{2{multiplexer_5_out[28]}}, multiplexer_7_out}),
    .in_1({{2{multiplexer_6_out[28]}}, multiplexer_8_out}), .out(multiplexer_9_out));
  Multiplexer #(.Bits(29)) multiplexer_10 (
    .sel(comparator_1_lt), .in_0({{2{multiplexer_6_out[28]}}, multiplexer_8_out}),
    .in_1({{2{multiplexer_5_out[28]}}, multiplexer_7_out}), .out(multiplexer_10_out));
  Sub #(.Bits(29)) sub_2 (
    .a(multiplexer_9_out), .b(multiplexer_10_out), .c_i(1'b0), .s({S[31], sub_2_s}));  // open: c_o
  assign not_3_out = ~sub_2_s;  // Not not_3, 28 bits wide
  Add #(.Bits(28)) add_3 (.a(not_3_out), .b({28{1'b0}}), .c_i(1'b1), .s(add_3_s));  // open: c_o
  Multiplexer #(.Bits(28)) multiplexer_11 (.sel(S[31]), .in_0(sub_2_s), .in_1(add_3_s), .out(multiplexer_11_out));
  or or_6 (or_6_out, multiplexer_11_out[0], multiplexer_11_out[1], multiplexer_11_out[3]);
  and and_1 (and_1_out, or_6_out, multiplexer_11_out[2]);
  Add #(.Bits(25)) add_4 (.a(multiplexer_11_out[27:3]), .b({25{1'b0}}), .c_i(1'b1), .s(add_4_s));  // open: c_o
  Multiplexer #(.Bits(25)) multiplexer_12 (
    .sel(and_1_out), .in_0(multiplexer_11_out[27:3]), .in_1(add_4_s), .out(multiplexer_12_out));
  PriorityEncoder #(.Selector_Bits(5)) priorityencoder_1 (
    .in0(multiplexer_12_out[0]), .in1(multiplexer_12_out[1]), .in2(multiplexer_12_out[2]),
    .in3(multiplexer_12_out[3]), .in4(multiplexer_12_out[4]), .in5(multiplexer_12_out[5]),
    .in6(multiplexer_12_out[6]), .in7(multiplexer_12_out[7]), .in8(multiplexer_12_out[8]),
    .in9(multiplexer_12_out[9]), .in10(multiplexer_12_out[10]), .in11(multiplexer_12_out[11]),
    .in12(multiplexer_12_out[12]), .in13(multiplexer_12_out[13]), .in14(multiplexer_12_out[14]),
    .in15(multiplexer_12_out[15]), .in16(multiplexer_12_out[16]), .in17(multiplexer_12_out[17]),
    .in18(multiplexer_12_out[18]), .in19(multiplexer_12_out[19]), .in20(multiplexer_12_out[20]),
    .in21(multiplexer_12_out[21]), .in22(multiplexer_12_out[22]), .in23(multiplexer_12_out[23]),
    .in24(multiplexer_12_out[24]), .in25(1'b0), .in26(1'b0), .in27(1'b0), .in28(1'b0), .in29(1'b0),
    .in30(1'b0), .in31(1'b0), .num(priorityencoder_1_num));  // open: any
  nor nor_1 (nor_1_out, multiplexer_12_out[24], multiplexer_12_out[23], multiplexer_12_out[22], multiplexer_12_out[21], multiplexer_12_out[20], multiplexer_12_out[19], multiplexer_12_out[18], multiplexer_12_out[17], multiplexer_12_out[16], multiplexer_12_out[15], multiplexer_12_out[14], multiplexer_12_out[13], multiplexer_12_out[12], multiplexer_12_out[11], multiplexer_12_out[10], multiplexer_12_out[9], multiplexer_12_out[8], multiplexer_12_out[7], multiplexer_12_out[6], multiplexer_12_out[5], multiplexer_12_out[4], multiplexer_12_out[3], multiplexer_12_out[2], multiplexer_12_out[1], multiplexer_12_out[0]);
  BarrelShifter #(.Bits(25), .barrelSigned("true")) barrelshifter_2 (
    .in(multiplexer_12_out), .shift(sub_3_s), .out(barrelshifter_2_out));
  Sub #(.Bits(6)) sub_3 (.a(6'b010111), .b({1'b0, priorityencoder_1_num}), .c_i(1'b0), .s(sub_3_s));  // open: c_o
  BitExtender #(.inputBits(6), .outputBits(8)) bitextender_1 (.in(sub_3_s), .out(bitextender_1_out));
  and and_2 (and_2_out, L[23], L[24], L[25], L[26], L[27], L[28], L[29], L[30]);
  and and_3 (and_3_out, R[23], R[24], R[25], R[26], R[27], R[28], R[29], R[30]);
  Sub #(.Bits(8)) sub_4 (.a(larger), .b(bitextender_1_out), .c_i(1'b0), .s(sub_4_s));  // open: c_o
  nor nor_2 (nor_2_out, and_2_out, and_3_out);
  and and_4 (and_4_out, and_2_out, NaN_A);
  or or_7 (or_7_out, and_2_out, and_3_out);
  and and_5 (and_5_out, NaN_B, and_3_out);
  Multiplexer #(.Bits(8)) multiplexer_13 (.sel(nor_1_out), .in_0(sub_4_s), .in_1({8{1'b0}}), .out(multiplexer_13_out));
  nor nor_3 (nor_3_out, nor_2_out, and_4_out, and_5_out);
  Multiplexer #(.Bits(23)) multiplexer_14 (
    .sel(nor_3_out), .in_0(barrelshifter_2_out[22:0]), .in_1({23{1'b0}}), .out(S[22:0]));
  Multiplexer #(.Bits(8)) multiplexer_15 (.sel(or_7_out), .in_0(multiplexer_13_out), .in_1({8{1'b1}}), .out(S[30:23]));

  // Other names for the same wires on the sheet: sign = S[31]; A[7:0] = L[30:23]; B[7:0] = R[30:23]
endmodule
