// Digital circuit GPU.dig as structural Verilog
module GPU (
  input  CC,
  input  C,
  input  [31:0] Din,
  input  [23:0] A,
  input  [1:0] funct3,
  input  WE,
  input  en,
  output [31:0] D,
  output [6:0] col
);

  wire Apos_0, Apos_1, ASCIIptr_0, ASCIIptr_1, b, exe, h, onecolor_0, onecolor_1, onecolor_2, onecolor_3,
       or_1_out, or_2_out, plotASCII, plotASCII_en, plotASCII_gen, plotLine, plotLine_en, plotRect,
       plotRect_en, pos_0, pos_1, pos_2, pos_3, str, str_0, str_0_Apos_0, str_0_Apos_1, str_0_ASCIIptr_0,
       str_0_ASCIIptr_1, str_0_onecolor_0, str_0_onecolor_1, str_0_onecolor_2, str_0_onecolor_3, str_0_pos_0,
       str_0_pos_1, str_0_pos_2, str_0_pos_3, str_1, str_1_Apos_0, str_1_Apos_1, str_1_ASCIIptr_0,
       str_1_ASCIIptr_1, str_1_onecolor_0, str_1_onecolor_1, str_1_onecolor_2, str_1_onecolor_3, str_1_pos_0,
       str_1_pos_1, str_1_pos_2, str_1_pos_3, str_2, str_2_Apos_0, str_2_Apos_1, str_2_ASCIIptr_0,
       str_2_ASCIIptr_1, str_2_onecolor_0, str_2_onecolor_1, str_2_onecolor_2, str_2_onecolor_3, str_2_pos_0,
       str_2_pos_1, str_2_pos_2, str_2_pos_3, str_3_Apos_0, str_3_Apos_1, str_3_ASCIIptr_0, str_3_ASCIIptr_1,
       str_3_onecolor_0, str_3_onecolor_1, str_3_onecolor_2, str_3_onecolor_3, str_3_pos_1, str_3_pos_2,
       str_3_pos_3, w;
  wire [0:0] Q_en;
  wire [7:0] D_Apos_0, D_Apos_1, D_ASCIIptr_0, D_ASCIIptr_1, D_exe, D_onecolor_0, D_onecolor_1, D_onecolor_2,
       D_onecolor_3, D_pos_0, D_pos_1, D_pos_2, D_pos_3, Din_0_D_Apos_0, Din_0_D_Apos_1, Din_0_D_ASCIIptr_0,
       Din_0_D_ASCIIptr_1, Din_0_D_onecolor_0, Din_0_D_onecolor_1, Din_0_D_onecolor_2, Din_0_D_onecolor_3,
       Din_0_D_pos_0, Din_0_D_pos_1, Din_0_D_pos_2, Din_0_D_pos_3, Din_1_D_Apos_0, Din_1_D_Apos_1,
       Din_1_D_ASCIIptr_0, Din_1_D_ASCIIptr_1, Din_1_D_onecolor_0, Din_1_D_onecolor_1, Din_1_D_onecolor_2,
       Din_1_D_onecolor_3, Din_1_D_pos_0, Din_1_D_pos_1, Din_1_D_pos_2, Din_1_D_pos_3, Din_2_D_Apos_0,
       Din_2_D_Apos_1, Din_2_D_ASCIIptr_0, Din_2_D_ASCIIptr_1, Din_2_D_onecolor_0, Din_2_D_onecolor_1,
       Din_2_D_onecolor_2, Din_2_D_onecolor_3, Din_2_D_pos_0, Din_2_D_pos_1, Din_2_D_pos_2, Din_2_D_pos_3,
       Din_3_D_Apos_0, Din_3_D_Apos_1, Din_3_D_ASCIIptr_0, Din_3_D_ASCIIptr_1, Din_3_D_onecolor_0,
       Din_3_D_onecolor_1, Din_3_D_onecolor_2, Din_3_D_onecolor_3, Din_3_D_pos_1, Din_3_D_pos_2,
       Din_3_D_pos_3, Q_Apos_0, Q_Apos_1, Q_ASCIIptr0, Q_ASCIIptr1, Q_onecolor1, Q_onecolor2, Q_onecolor3,
       Q_pos0, Q_pos1, Q_pos2, Q_pos3;
  wire [7:7] Q_onecolor0;
  wire [8:0] dx, dy;
  wire [15:0] driver_1_out, plotascii_1_addr, plotline_1_addr, plotrect_1_addr;

  Demultiplexer #(.Selector_Bits(3)) demultiplexer_1 (
    .sel(D_exe[2:0]), .in(exe), .out_0(plotLine), .out_1(plotRect), .out_2(plotASCII));  // open: out_3, out_4, out_5, out_6, out_7
  Register #(.Bits(8)) register_1 (.D(D_pos_0), .C(C), .en(pos_0), .Q(Q_pos0));
  Register #(.Bits(8)) register_2 (.D(D_pos_1), .C(C), .en(pos_1), .Q(Q_pos1));
  Register #(.Bits(8)) register_3 (.D(D_pos_2), .C(C), .en(pos_2), .Q(Q_pos2));
  Register #(.Bits(8)) register_4 (.D(D_pos_3), .C(C), .en(pos_3), .Q(Q_pos3));
  Register #(.Bits(8)) register_5 (.D(D_onecolor_0), .C(C), .en(onecolor_0), .Q({Q_onecolor0[7], col}));
  Register #(.Bits(8)) register_6 (.D(D_onecolor_1), .C(C), .en(onecolor_1), .Q(Q_onecolor1));
  Register #(.Bits(8)) register_7 (.D(D_onecolor_2), .C(C), .en(onecolor_2), .Q(Q_onecolor2));
  Register #(.Bits(8)) register_8 (.D(D_onecolor_3), .C(C), .en(onecolor_3), .Q(Q_onecolor3));
  Register #(.Bits(8)) register_9 (.D(D_Apos_0), .C(C), .en(Apos_0), .Q(Q_Apos_0));
  Register #(.Bits(8)) register_10 (.D(D_Apos_1), .C(C), .en(Apos_1), .Q(Q_Apos_1));
  Register #(.Bits(8)) register_11 (.D(D_ASCIIptr_0), .C(C), .en(ASCIIptr_0), .Q(Q_ASCIIptr0));
  Register #(.Bits(8)) register_12 (.D(D_ASCIIptr_1), .C(C), .en(ASCIIptr_1), .Q(Q_ASCIIptr1));
  plotLine plotline_1 (
    .set(plotLine), .dx(dx), .dy(dy), .x_0(Q_pos0), .y_0(Q_pos1), .CC(CC), .addr(plotline_1_addr),
    .en(plotLine_en));
  plotRect plotrect_1 (
    .set(plotRect), .dx(dx), .dy(dy), .x_0(Q_pos0), .y_0(Q_pos1), .x_1(Q_pos2), .CC(CC),
    .addr(plotrect_1_addr), .en(plotRect_en));
  plotASCII plotascii_1 (
    .set(plotASCII), .x_0(Q_Apos_0), .y_0(Q_Apos_1), .ASCIIptr(Q_ASCIIptr0), .CC(CC),
    .addr(plotascii_1_addr), .en(plotASCII_en), .gen(plotASCII_gen));
  Sub #(.Bits(9)) sub_1 (.a({1'b0, Q_pos2}), .b({1'b0, Q_pos0}), .c_i(1'b0), .s(dx));  // open: c_o
  assign driver_1_out = plotLine_en ? plotline_1_addr : 16'bz;  // Driver driver_1
  assign driver_1_out = plotRect_en ? plotrect_1_addr : 16'bz;  // Driver driver_2
  assign driver_1_out = plotASCII_en ? plotascii_1_addr : 16'bz;  // Driver driver_3
  and and_1 (b, ~funct3[0], ~funct3[1]);  // And
  and and_2 (h, funct3[0], ~funct3[1]);  // And
  and and_3 (w, ~funct3[0], funct3[1]);  // And
  or or_1 (or_1_out, b, h, w);
  or or_2 (or_2_out, h, w);
  Sub #(.Bits(9)) sub_2 (.a({1'b0, Q_pos3}), .b({1'b0, Q_pos1}), .c_i(1'b0), .s(dy));  // open: c_o
  GraphicCard #(.graphicHeight(256), .graphicWidth(256), .Bits(7)) graphiccard_1 (
    .A({1'b0, driver_1_out}), .str(str), .C(CC), .ld(1'b0), .B(1'b0), .D(col));
  or or_3 (Q_en[0], plotLine_en, plotRect_en, plotASCII_en);
  or or_4 (str, plotLine_en, plotRect_en, plotASCII_gen);
  and and_4 (str_0, en, WE, or_1_out);
  and and_5 (str_1, en, WE, or_2_out);
  and and_6 (str_2, en, WE, w);
  assign D_pos_0 = Din_0_D_pos_0 | Din_1_D_pos_0 | Din_2_D_pos_0;  // Or or_5, 8 bits wide
  assign D_pos_1 = Din_0_D_pos_1 | Din_1_D_pos_1 | Din_2_D_pos_1 | Din_3_D_pos_1;  // Or or_6, 8 bits wide
  assign D_pos_2 = Din_0_D_pos_2 | Din_1_D_pos_2 | Din_2_D_pos_2 | Din_3_D_pos_2;  // Or or_7, 8 bits wide
  assign D_pos_3 = Din_0_D_pos_3 | Din_1_D_pos_3 | Din_2_D_pos_3 | Din_3_D_pos_3;  // Or or_8, 8 bits wide
  assign D_onecolor_0 = Din_0_D_onecolor_0 | Din_1_D_onecolor_0 | Din_2_D_onecolor_0 | Din_3_D_onecolor_0;  // Or or_9, 8 bits wide
  assign D_onecolor_1 = Din_0_D_onecolor_1 | Din_1_D_onecolor_1 | Din_2_D_onecolor_1 | Din_3_D_onecolor_1;  // Or or_10, 8 bits wide
  assign D_onecolor_2 = Din_0_D_onecolor_2 | Din_1_D_onecolor_2 | Din_2_D_onecolor_2 | Din_3_D_onecolor_2;  // Or or_11, 8 bits wide
  assign D_onecolor_3 = Din_0_D_onecolor_3 | Din_1_D_onecolor_3 | Din_2_D_onecolor_3 | Din_3_D_onecolor_3;  // Or or_12, 8 bits wide
  assign D_ASCIIptr_0 = Din_0_D_ASCIIptr_0 | Din_1_D_ASCIIptr_0 | Din_2_D_ASCIIptr_0 | Din_3_D_ASCIIptr_0;  // Or or_13, 8 bits wide
  assign D_ASCIIptr_1 = Din_0_D_ASCIIptr_1 | Din_1_D_ASCIIptr_1 | Din_2_D_ASCIIptr_1 | Din_3_D_ASCIIptr_1;  // Or or_14, 8 bits wide
  assign D_Apos_0 = Din_0_D_Apos_0 | Din_1_D_Apos_0 | Din_2_D_Apos_0 | Din_3_D_Apos_0;  // Or or_15, 8 bits wide
  assign D_Apos_1 = Din_0_D_Apos_1 | Din_1_D_Apos_1 | Din_2_D_Apos_1 | Din_3_D_Apos_1;  // Or or_16, 8 bits wide
  Demultiplexer #(.Selector_Bits(5), .Bits(8)) demultiplexer_2 (
    .sel(A[4:0]), .in(Din[7:0]), .out_0(D_exe), .out_2(Din_0_D_pos_0), .out_3(Din_0_D_pos_1),
    .out_4(Din_0_D_pos_2), .out_5(Din_0_D_pos_3), .out_6(Din_0_D_onecolor_0), .out_7(Din_0_D_onecolor_1),
    .out_8(Din_0_D_onecolor_2), .out_9(Din_0_D_onecolor_3), .out_10(Din_0_D_ASCIIptr_0),
    .out_11(Din_0_D_ASCIIptr_1), .out_12(Din_0_D_Apos_0), .out_13(Din_0_D_Apos_1));  // open: out_1, out_14, out_15, out_16, out_17, out_18, out_19, out_20, out_21, out_22, out_23, out_24, out_25, out_26, out_27, out_28, out_29, out_30, out_31
  Demultiplexer #(.Selector_Bits(5), .Bits(8)) demultiplexer_3 (
    .sel(A[4:0]), .in(Din[23:16]), .out_0(Din_2_D_pos_0), .out_1(Din_2_D_pos_1), .out_2(Din_2_D_pos_2),
    .out_3(Din_2_D_pos_3), .out_4(Din_2_D_onecolor_0), .out_5(Din_2_D_onecolor_1),
    .out_6(Din_2_D_onecolor_2), .out_7(Din_2_D_onecolor_3), .out_8(Din_2_D_ASCIIptr_0),
    .out_9(Din_2_D_ASCIIptr_1), .out_10(Din_2_D_Apos_0), .out_11(Din_2_D_Apos_1));  // open: out_12, out_13, out_14, out_15, out_16, out_17, out_18, out_19, out_20, out_21, out_22, out_23, out_24, out_25, out_26, out_27, out_28, out_29, out_30, out_31
  or or_17 (pos_0, str_0_pos_0, str_1_pos_0, str_2_pos_0);
  or or_18 (pos_1, str_0_pos_1, str_1_pos_1, str_2_pos_1, str_3_pos_1);
  Demultiplexer #(.Selector_Bits(5), .Bits(8)) demultiplexer_4 (
    .sel(A[4:0]), .in(Din[15:8]), .out_1(Din_1_D_pos_0), .out_2(Din_1_D_pos_1), .out_3(Din_1_D_pos_2),
    .out_4(Din_1_D_pos_3), .out_5(Din_1_D_onecolor_0), .out_6(Din_1_D_onecolor_1),
    .out_7(Din_1_D_onecolor_2), .out_8(Din_1_D_onecolor_3), .out_9(Din_1_D_ASCIIptr_0),
    .out_10(Din_1_D_ASCIIptr_1), .out_11(Din_1_D_Apos_0), .out_12(Din_1_D_Apos_1));  // open: out_0, out_13, out_14, out_15, out_16, out_17, out_18, out_19, out_20, out_21, out_22, out_23, out_24, out_25, out_26, out_27, out_28, out_29, out_30, out_31
  Demultiplexer #(.Selector_Bits(5), .Bits(8)) demultiplexer_5 (
    .sel(A[4:0]), .in(Din[31:24]), .out_0(Din_3_D_pos_1), .out_1(Din_3_D_pos_2), .out_2(Din_3_D_pos_3),
    .out_3(Din_3_D_onecolor_0), .out_4(Din_3_D_onecolor_1), .out_5(Din_3_D_onecolor_2),
    .out_6(Din_3_D_onecolor_3), .out_7(Din_3_D_ASCIIptr_0), .out_8(Din_3_D_ASCIIptr_1),
    .out_9(Din_3_D_Apos_0), .out_10(Din_3_D_Apos_1));  // open: out_11, out_12, out_13, out_14, out_15, out_16, out_17, out_18, out_19, out_20, out_21, out_22, out_23, out_24, out_25, out_26, out_27, out_28, out_29, out_30, out_31
  or or_19 (pos_2, str_0_pos_2, str_1_pos_2, str_2_pos_2, str_3_pos_2);
  or or_20 (pos_3, str_0_pos_3, str_1_pos_3, str_2_pos_3, str_3_pos_3);
  Demultiplexer #(.Selector_Bits(5)) demultiplexer_6 (
    .sel(A[4:0]), .in(str_0), .out_0(exe), .out_2(str_0_pos_0), .out_3(str_0_pos_1), .out_4(str_0_pos_2),
    .out_5(str_0_pos_3), .out_6(str_0_onecolor_0), .out_7(str_0_onecolor_1), .out_8(str_0_onecolor_2),
    .out_9(str_0_onecolor_3), .out_10(str_0_ASCIIptr_0), .out_11(str_0_ASCIIptr_1), .out_12(str_0_Apos_0),
    .out_13(str_0_Apos_1));  // open: out_1, out_14, out_15, out_16, out_17, out_18, out_19, out_20, out_21, out_22, out_23, out_24, out_25, out_26, out_27, out_28, out_29, out_30, out_31
  Demultiplexer #(.Selector_Bits(5)) demultiplexer_7 (
    .sel(A[4:0]), .in(str_2), .out_0(str_2_pos_0), .out_1(str_2_pos_1), .out_2(str_2_pos_2),
    .out_3(str_2_pos_3), .out_4(str_2_onecolor_0), .out_5(str_2_onecolor_1), .out_6(str_2_onecolor_2),
    .out_7(str_2_onecolor_3), .out_8(str_2_ASCIIptr_0), .out_9(str_2_ASCIIptr_1), .out_10(str_2_Apos_0),
    .out_11(str_2_Apos_1));  // open: out_12, out_13, out_14, out_15, out_16, out_17, out_18, out_19, out_20, out_21, out_22, out_23, out_24, out_25, out_26, out_27, out_28, out_29, out_30, out_31
  or or_21 (onecolor_0, str_0_onecolor_0, str_1_onecolor_0, str_2_onecolor_0, str_3_onecolor_0);
  or or_22 (onecolor_1, str_0_onecolor_1, str_1_onecolor_1, str_2_onecolor_1, str_3_onecolor_1);
  Demultiplexer #(.Selector_Bits(5)) demultiplexer_8 (
    .sel(A[4:0]), .in(str_1), .out_1(str_1_pos_0), .out_2(str_1_pos_1), .out_3(str_1_pos_2),
    .out_4(str_1_pos_3), .out_5(str_1_onecolor_0), .out_6(str_1_onecolor_1), .out_7(str_1_onecolor_2),
    .out_8(str_1_onecolor_3), .out_9(str_1_ASCIIptr_0), .out_10(str_1_ASCIIptr_1), .out_11(str_1_Apos_0),
    .out_12(str_1_Apos_1));  // open: out_0, out_13, out_14, out_15, out_16, out_17, out_18, out_19, out_20, out_21, out_22, out_23, out_24, out_25, out_26, out_27, out_28, out_29, out_30, out_31
  Demultiplexer #(.Selector_Bits(5)) demultiplexer_9 (
    .sel(A[4:0]), .in(str_2), .out_0(str_3_pos_1), .out_1(str_3_pos_2), .out_2(str_3_pos_3),
    .out_3(str_3_onecolor_0), .out_4(str_3_onecolor_1), .out_5(str_3_onecolor_2), .out_6(str_3_onecolor_3),
    .out_7(str_3_ASCIIptr_0), .out_8(str_3_ASCIIptr_1), .out_9(str_3_Apos_0), .out_10(str_3_Apos_1));  // open: out_11, out_12, out_13, out_14, out_15, out_16, out_17, out_18, out_19, out_20, out_21, out_22, out_23, out_24, out_25, out_26, out_27, out_28, out_29, out_30, out_31
  or or_23 (onecolor_2, str_0_onecolor_2, str_1_onecolor_2, str_2_onecolor_2, str_3_onecolor_2);
  or or_24 (onecolor_3, str_0_onecolor_3, str_1_onecolor_3, str_2_onecolor_3, str_3_onecolor_3);
  or or_25 (ASCIIptr_0, str_0_ASCIIptr_0, str_1_ASCIIptr_0, str_2_ASCIIptr_0, str_3_ASCIIptr_0);
  Multiplexer #(.Selector_Bits(5), .Bits(8)) multiplexer_1 (
    .sel(A[4:0]), .in_0({{5{1'b0}}, D_exe[2:0]}), .in_1({{7{1'b0}}, Q_en[0]}), .in_2(Q_pos0), .in_3(Q_pos1),
    .in_4(Q_pos2), .in_5(Q_pos3), .in_6({Q_onecolor0[7], col}), .in_7(Q_onecolor1), .in_8(Q_onecolor2),
    .in_9(Q_onecolor3), .in_10(Q_ASCIIptr0), .in_11(Q_ASCIIptr1), .in_12(Q_Apos_0), .in_13(Q_Apos_1),
    .in_14({8{1'b0}}), .in_15({8{1'b0}}), .in_16({8{1'b0}}), .in_17({8{1'b0}}), .in_18({8{1'b0}}),
    .in_19({8{1'b0}}), .in_20({8{1'b0}}), .in_21({8{1'b0}}), .in_22({8{1'b0}}), .in_23({8{1'b0}}),
    .in_24({8{1'b0}}), .in_25({8{1'b0}}), .in_26({8{1'b0}}), .in_27({8{1'b0}}), .in_28({8{1'b0}}),
    .in_29({8{1'b0}}), .in_30({8{1'b0}}), .in_31({8{1'b0}}), .out(D[7:0]));
  Multiplexer #(.Selector_Bits(5), .Bits(8)) multiplexer_2 (
    .sel(A[4:0]), .in_0(Q_pos0), .in_1(Q_pos1), .in_2(Q_pos2), .in_3(Q_pos3), .in_4({Q_onecolor0[7], col}),
    .in_5(Q_onecolor1), .in_6(Q_onecolor2), .in_7(Q_onecolor3), .in_8(Q_ASCIIptr0), .in_9(Q_ASCIIptr1),
    .in_10(Q_Apos_0), .in_11(Q_Apos_1), .in_12({8{1'b0}}), .in_13({8{1'b0}}), .in_14({8{1'b0}}),
    .in_15({8{1'b0}}), .in_16({8{1'b0}}), .in_17({8{1'b0}}), .in_18({8{1'b0}}), .in_19({8{1'b0}}),
    .in_20({8{1'b0}}), .in_21({8{1'b0}}), .in_22({8{1'b0}}), .in_23({8{1'b0}}), .in_24({8{1'b0}}),
    .in_25({8{1'b0}}), .in_26({8{1'b0}}), .in_27({8{1'b0}}), .in_28({8{1'b0}}), .in_29({8{1'b0}}),
    .in_30({8{1'b0}}), .in_31({8{1'b0}}), .out(D[23:16]));
  or or_26 (ASCIIptr_1, str_0_ASCIIptr_1, str_1_ASCIIptr_1, str_2_ASCIIptr_1, str_3_ASCIIptr_1);
  or or_27 (Apos_0, str_0_Apos_0, str_1_Apos_0, str_2_Apos_0, str_3_Apos_0);
  Multiplexer #(.Selector_Bits(5), .Bits(8)) multiplexer_3 (
    .sel(A[4:0]), .in_0({{7{1'b0}}, Q_en[0]}), .in_1(Q_pos0), .in_2(Q_pos1), .in_3(Q_pos2), .in_4(Q_pos3),
    .in_5({Q_onecolor0[7], col}), .in_6(Q_onecolor1), .in_7(Q_onecolor2), .in_8(Q_onecolor3),
    .in_9(Q_ASCIIptr0), .in_10(Q_ASCIIptr1), .in_11(Q_Apos_0), .in_12(Q_Apos_1), .in_13({8{1'b0}}),
    .in_14({8{1'b0}}), .in_15({8{1'b0}}), .in_16({8{1'b0}}), .in_17({8{1'b0}}), .in_18({8{1'b0}}),
    .in_19({8{1'b0}}), .in_20({8{1'b0}}), .in_21({8{1'b0}}), .in_22({8{1'b0}}), .in_23({8{1'b0}}),
    .in_24({8{1'b0}}), .in_25({8{1'b0}}), .in_26({8{1'b0}}), .in_27({8{1'b0}}), .in_28({8{1'b0}}),
    .in_29({8{1'b0}}), .in_30({8{1'b0}}), .in_31({8{1'b0}}), .out(D[15:8]));
  Multiplexer #(.Selector_Bits(5), .Bits(8)) multiplexer_4 (
    .sel(A[4:0]), .in_0(Q_pos1), .in_1(Q_pos2), .in_2(Q_pos3), .in_3({Q_onecolor0[7], col}),
    .in_4(Q_onecolor1), .in_5(Q_onecolor2), .in_6(Q_onecolor3), .in_7(Q_ASCIIptr0), .in_8(Q_ASCIIptr1),
    .in_9(Q_Apos_0), .in_10(Q_Apos_1), .in_11({8{1'b0}}), .in_12({8{1'b0}}), .in_13({8{1'b0}}),
    .in_14({8{1'b0}}), .in_15({8{1'b0}}), .in_16({8{1'b0}}), .in_17({8{1'b0}}), .in_18({8{1'b0}}),
    .in_19({8{1'b0}}), .in_20({8{1'b0}}), .in_21({8{1'b0}}), .in_22({8{1'b0}}), .in_23({8{1'b0}}),
    .in_24({8{1'b0}}), .in_25({8{1'b0}}), .in_26({8{1'b0}}), .in_27({8{1'b0}}), .in_28({8{1'b0}}),
    .in_29({8{1'b0}}), .in_30({8{1'b0}}), .in_31({8{1'b0}}), .out(D[31:24]));
  or or_28 (Apos_1, str_0_Apos_1, str_1_Apos_1, str_2_Apos_1, str_3_Apos_1);

  // Other names for the same wires on the sheet: D_0[7:0] = D[7:0]; D_1[7:0] = D[15:8]; D_2[7:0] = D[23:16];
  //   D_3[7:0] = D[31:24]; Q_exe[2:0] = D_exe[2:0]; Din_0[7:0] = Din[7:0]; Din_1[7:0] = Din[15:8];
  //   Din_2[7:0] = Din[23:16]; Din_3[7:0] = Din[31:24]; Q_onecolor0[6:0] = col

  // Notes on the sheet:
  //   CC: Hz: 2147483647
  //   C: Hz: 2
  //   x_0
  //   y_0
  //   x_1
  //   y_1
endmodule
