// Digital circuit GameControllerIO.dig as structural Verilog
module GameControllerIO (
  input  [31:0] _1P,
  input  [31:0] _2P,
  input  [31:0] _3P,
  input  [31:0] _4P,
  input  C,
  input  [23:0] A,
  output [31:0] D
);

  wire [7:0] D_0, D_1, D_2, D_3, D_4, D_5, D_6, D_7, D_8, D_9, D_10, D_11, D_12, D_13, D_14, D_15;

  D_FF #(.Bits(32)) d_ff_1 (.D(_1P), .C(C), .Q({D_3, D_2, D_1, D_0}));  // open: nQ
  D_FF #(.Bits(32)) d_ff_2 (.D(_2P), .C(C), .Q({D_7, D_6, D_5, D_4}));  // open: nQ
  D_FF #(.Bits(32)) d_ff_3 (.D(_3P), .C(C), .Q({D_11, D_10, D_9, D_8}));  // open: nQ
  D_FF #(.Bits(32)) d_ff_4 (.D(_4P), .C(C), .Q({D_15, D_14, D_13, D_12}));  // open: nQ
  Multiplexer #(.Selector_Bits(4), .Bits(8)) multiplexer_1 (
    .sel(A[3:0]), .in_0(D_0), .in_1(D_1), .in_2(D_2), .in_3(D_3), .in_4(D_4), .in_5(D_5), .in_6(D_6),
    .in_7(D_7), .in_8(D_8), .in_9(D_9), .in_10(D_10), .in_11(D_11), .in_12(D_12), .in_13(D_13), .in_14(D_14),
    .in_15(D_15), .out(D[7:0]));
  Multiplexer #(.Selector_Bits(4), .Bits(8)) multiplexer_2 (
    .sel(A[3:0]), .in_0(D_2), .in_1(D_3), .in_2(D_4), .in_3(D_5), .in_4(D_6), .in_5(D_7), .in_6(D_8),
    .in_7(D_9), .in_8(D_10), .in_9(D_11), .in_10(D_12), .in_11(D_13), .in_12(D_14), .in_13(D_15),
    .in_14({8{1'b0}}), .in_15({8{1'b0}}), .out(D[23:16]));
  Multiplexer #(.Selector_Bits(4), .Bits(8)) multiplexer_3 (
    .sel(A[3:0]), .in_0(D_1), .in_1(D_2), .in_2(D_3), .in_3(D_4), .in_4(D_5), .in_5(D_6), .in_6(D_7),
    .in_7(D_8), .in_8(D_9), .in_9(D_10), .in_10(D_11), .in_11(D_12), .in_12(D_13), .in_13(D_14),
    .in_14(D_15), .in_15({8{1'b0}}), .out(D[15:8]));
  Multiplexer #(.Selector_Bits(4), .Bits(8)) multiplexer_4 (
    .sel(A[3:0]), .in_0(D_3), .in_1(D_4), .in_2(D_5), .in_3(D_6), .in_4(D_7), .in_5(D_8), .in_6(D_9),
    .in_7(D_10), .in_8(D_11), .in_9(D_12), .in_10(D_13), .in_11(D_14), .in_12(D_15), .in_13({8{1'b0}}),
    .in_14({8{1'b0}}), .in_15({8{1'b0}}), .out(D[31:24]));

  // Other names for the same wires on the sheet: B_0[7:0] = D[7:0]; B_1[7:0] = D[15:8]; B_2[7:0] = D[23:16];
  //   B_3[7:0] = D[31:24]
endmodule
