// Digital circuit Instr_Decorder.dig as structural Verilog
module Instr_Decorder (
  input  [31:0] instr,
  output jump,
  output branch,
  output AddressSrc,
  output MemSrc,
  output ExeSrc,
  output floatRegWrite,
  output FPUSrc,
  output [4:0] FPUCtrl,
  output [4:0] ALUCtrl,
  output RegWrite,
  output [2:0] ImmSrc,
  output ALUSrc,
  output [1:0] ResultSrc,
  output JumpSrc,
  output MemWrite,
  output [2:0] funct3,
  output [4:0] rs1,
  output [4:0] rs2,
  output [4:0] rd,
  output [24:0] imm
);

  wire alu, alui, and_15_out, and_22_out, auipc, f2int, fcomp, fload, fpu, funct3_000, funct3_001,
       funct3_010, funct3_101, jal, jalr, load, lui, or_1_out, or_2_out, or_3_out, or_4_out, store;
  wire [1:0] multiplexer_2_out;

  and and_1 (load, instr[0], instr[1], ~instr[2], ~instr[3], ~instr[4], ~instr[5], ~instr[6]);  // And
  and and_2 (alui, instr[0], instr[1], ~instr[2], ~instr[3], instr[4], ~instr[5], ~instr[6]);  // And
  and and_3 (store, instr[0], instr[1], ~instr[2], ~instr[3], ~instr[4], instr[5], ~instr[6]);  // And
  and and_4 (lui, instr[0], instr[1], instr[2], ~instr[3], instr[4], instr[5], ~instr[6]);  // And
  and and_5 (auipc, instr[0], instr[1], instr[2], ~instr[3], instr[4], ~instr[5], ~instr[6]);  // And
  and and_6 (ImmSrc[2], ~instr[0], ~instr[1], instr[2], ~instr[3], instr[4], ~instr[5], ~instr[6]);  // And
  or or_1 (or_1_out, funct3_001, funct3_101);
  Multiplexer #(.Bits(5)) multiplexer_1 (.sel(lui), .in_0(instr[19:15]), .in_1({5{1'b0}}), .out(rs1));
  and and_7 (alu, instr[0], instr[1], ~instr[2], ~instr[3], instr[4], instr[5], ~instr[6]);  // And
  and and_8 (branch, instr[0], instr[1], ~instr[2], ~instr[3], ~instr[4], instr[5], instr[6]);  // And
  and and_9 (jalr, instr[0], instr[1], instr[2], ~instr[3], ~instr[4], instr[5], instr[6]);  // And
  and and_10 (jal, instr[0], instr[1], instr[2], instr[3], ~instr[4], instr[5], instr[6]);  // And
  and and_11 (funct3_001, instr[12], ~instr[13], ~instr[14]);  // And
  and and_12 (funct3_101, instr[12], ~instr[13], instr[14]);  // And
  and and_13 (funct3_000, ~instr[12], ~instr[13], ~instr[14]);  // And
  and and_14 (funct3_010, ~instr[12], instr[13], ~instr[14]);  // And
  and and_15 (and_15_out, or_1_out, alui);
  or or_2 (or_2_out, alu, and_15_out);
  Multiplexer #(.Bits(2)) multiplexer_2 (
    .sel(or_2_out), .in_0(2'b00), .in_1({instr[25], instr[30]}), .out(multiplexer_2_out));
  Multiplexer #(.Bits(3)) multiplexer_3 (.sel(ImmSrc[2]), .in_0(instr[14:12]), .in_1(3'b010), .out(funct3));
  or or_3 (or_3_out, lui, jalr, load, store, fload, MemSrc);
  and and_16 (fpu, instr[0], instr[1], ~instr[2], ~instr[3], instr[4], ~instr[5], instr[6]);  // And
  and and_17 (fload, instr[0], instr[1], instr[2], ~instr[3], ~instr[4], ~instr[5], ~instr[6]);  // And
  and and_18 (MemSrc, instr[0], instr[1], instr[2], ~instr[3], ~instr[4], instr[5], ~instr[6]);  // And
  and and_19 (fcomp, ~instr[0], ~instr[1], instr[2], ~instr[3], instr[4], ~instr[5], instr[6]);  // And
  and and_20 (f2int, instr[0], ~instr[1], instr[2], ~instr[3], instr[4], ~instr[5], instr[6]);  // And
  and and_21 (FPUSrc, ~instr[0], instr[1], instr[2], ~instr[3], instr[4], ~instr[5], instr[6]);  // And
  Multiplexer #(.Bits(5)) multiplexer_4 (
    .sel(or_3_out), .in_0({multiplexer_2_out, instr[14:12]}), .in_1({5{1'b0}}), .out(ALUCtrl));
  PriorityEncoder #(.Selector_Bits(2)) priorityencoder_1 (
    .in0(fpu), .in1(fcomp), .in2(f2int), .in3(FPUSrc), .num(FPUCtrl[4:3]));  // open: any
  or or_4 (or_4_out, load, store);
  nor nor_1 (RegWrite, store, branch, fpu, fload, MemSrc, FPUSrc);
  or or_5 (ImmSrc[0], store, lui, MemSrc, branch, auipc);
  or or_6 (ImmSrc[1], jal, auipc, lui);
  nor nor_2 (ALUSrc, alu, branch);
  nor nor_3 (ResultSrc[0], load, jalr, jal, fload);
  or or_7 (ResultSrc[1], jalr, auipc, jal);
  not not_1 (JumpSrc, jalr);
  or or_8 (MemWrite, store, MemSrc);
  or or_9 (jump, jalr, jal);
  nor nor_4 (ExeSrc, alui, alu, ImmSrc[2], lui, jalr);
  or or_10 (floatRegWrite, fpu, fload, FPUSrc);
  and and_22 (and_22_out, funct3_010, or_4_out);
  or or_11 (AddressSrc, and_22_out, fload, MemSrc);

  assign FPUCtrl[2:0] = instr[14:12];
  assign imm = instr[31:7];
  assign rd = instr[11:7];
  assign rs2 = instr[24:20];

  // Other names for the same wires on the sheet: aluui = ImmSrc[2]; fstore = MemSrc; op_0 = instr[0]; op_1 = instr[1];
  //   op_2 = instr[2]; op_3 = instr[3]; op_4 = instr[4]; op_5 = instr[5]; op_6 = instr[6]; funct3_0 = instr[12];
  //   funct3_1 = instr[13]; funct3_2 = instr[14]; int2f = FPUSrc

  // Notes on the sheet:
  //   op
  //   funct7
  //   funct3
endmodule
