// Digital circuit MergeData.dig as structural Verilog
module MergeData (
  input  [31:0] D,
  input  [31:0] imm,
  input  [2:0] funct3,
  output [31:0] RD
);

  wire [7:0] multiplexer_1_out;
  wire [15:0] multiplexer_2_out;

  Multiplexer #(.Selector_Bits(2), .Bits(8)) multiplexer_1 (
    .sel(imm[1:0]), .in_0(D[7:0]), .in_1(D[15:8]), .in_2(D[23:16]), .in_3(D[31:24]), .out(multiplexer_1_out));
  Multiplexer #(.Selector_Bits(2), .Bits(16)) multiplexer_2 (
    .sel(imm[1:0]), .in_0(D[15:0]), .in_1(D[31:16]), .in_2(D[15:0]), .in_3(D[31:16]), .out(multiplexer_2_out));
  Multiplexer #(.Selector_Bits(3), .Bits(32)) multiplexer_3 (
    .sel(funct3), .in_0({{25{multiplexer_1_out[7]}}, multiplexer_1_out[6:0]}),
    .in_1({{17{multiplexer_2_out[15]}}, multiplexer_2_out[14:0]}), .in_2(D), .in_3({32{1'b0}}),
    .in_4({{24{1'b0}}, multiplexer_1_out}), .in_5({{16{1'b0}}, multiplexer_2_out}), .in_6({32{1'b0}}),
    .in_7({32{1'b0}}), .out(RD));

  // Other names for the same wires on the sheet: imm_t[1:0] = imm[1:0]
endmodule
