// Digital circuit RAM.dig as structural Verilog
module RAM (
  input  WE,
  input  C,
  input  [23:0] _2A,
  output [31:0] R2D
);

  wire and_1_out, undriven;

  and and_1 (and_1_out, WE, undriven);
endmodule
