// Digital circuit RAMViewer.dig as structural Verilog
module RAMViewer (
  input  CC,
  input  [31:0] _2D,
  output [23:0] _2A
);

  wire [63:0] u_LEDmat_decorder_data;

  LEDmat_decorder #(.applicationType("GHDL"), .CodeFile("C:\\Users\\Gfla\\Documents\\GitHub\\RV32I\\RV32I\\LEDmat_decorder.vhd")) u_LEDmat_decorder (
    .raw(_2D[5:0]), .data(u_LEDmat_decorder_data));
  Counter #(.Bits(6)) counter_1 (.en(1'b1), .C(CC), .clr(1'b0), .out(_2A[5:0]));  // open: ovf
  LedMatrix #(.ledPersistence("true"), .colAddrBits(6), .rowDataBits(64)) ledmatrix_1 (
    .rows(u_LEDmat_decorder_data), .column(_2A[5:0]));

  assign _2A[23:6] = {18{1'b0}};

  // Notes on the sheet:
  //   CC: Hz: 50000
endmodule
