// Digital circuit RS-FF+.dig as structural Verilog
module RS_FF (
  input  S,
  input  C,
  input  R,
  output Q
);

  wire and_1_out, and_2_out, and_3_out, and_4_out, not_1_out, not_2_out, or_1_out, or_2_out, Q_1_n;

  not not_1 (not_1_out, R);
  not not_2 (not_2_out, Q_1_n);
  and and_1 (and_1_out, S, R, Q);
  and and_2 (and_2_out, S, Q_1_n);
  and and_3 (and_3_out, S, not_1_out, not_2_out);
  and and_4 (and_4_out, not_1_out, Q);
  or or_1 (or_1_out, and_1_out, and_2_out);
  or or_2 (or_2_out, and_3_out, and_4_out);
  D_FF u_Q_1_n (.D(or_1_out), .C(C), .Q(Q_1_n));  // open: nQ
  D_FF Q_0_n (.D(or_2_out), .C(C), .Q(Q));  // open: nQ

  // Other names for the same wires on the sheet: Q_0_n = Q

  // Notes on the sheet:
  //   C: Hz: 2
endmodule
