// Digital circuit Reg10bit.dig as structural Verilog
module Reg10bit (
  input  [9:0] D,
  input  en,
  input  C,
  input  [9:0] res_val,
  output [9:0] Q
);

  wire [9:0] multiplexer_1_out;

  Multiplexer #(.Bits(10)) multiplexer_1 (.sel(en), .in_0(res_val), .in_1(D), .out(multiplexer_1_out));
  D_FF #(.Bits(10)) d_ff_1 (.D(multiplexer_1_out), .C(C), .Q(Q));  // open: nQ
endmodule
