// Digital circuit Reg9bit.dig as structural Verilog
module Reg9bit (
  input  [8:0] D,
  input  en,
  input  C,
  input  [8:0] res_val,
  output [8:0] Q
);

  wire [8:0] multiplexer_1_out;

  Multiplexer #(.Bits(9)) multiplexer_1 (.sel(en), .in_0(res_val), .in_1(D), .out(multiplexer_1_out));
  D_FF #(.Bits(9)) d_ff_1 (.D(multiplexer_1_out), .C(C), .Q(Q));  // open: nQ
endmodule
