// Digital circuit int2float.dig as structural Verilog
module int2float (
  input  [31:0] L,
  output [31:0] f
);

  wire and_1_out, or_1_out, or_2_out, priorityencoder_1_any;
  wire [4:0] priorityencoder_1_num;
  wire [7:0] add_3_s;
  wire [22:0] add_2_s;
  wire [31:0] add_1_s, multiplexer_1_out, not_1_out;
  wire [63:0] barrelshifter_1_out;

  assign not_1_out = ~L;  // Not not_1, 32 bits wide
  Add #(.Bits(32)) add_1 (.a(not_1_out), .b({32{1'b0}}), .c_i(1'b1), .s(add_1_s));  // open: c_o
  Multiplexer #(.Bits(32)) multiplexer_1 (.sel(L[31]), .in_0(L), .in_1(add_1_s), .out(multiplexer_1_out));
  PriorityEncoder #(.Selector_Bits(5)) priorityencoder_1 (
    .in0(multiplexer_1_out[0]), .in1(multiplexer_1_out[1]), .in2(multiplexer_1_out[2]),
    .in3(multiplexer_1_out[3]), .in4(multiplexer_1_out[4]), .in5(multiplexer_1_out[5]),
    .in6(multiplexer_1_out[6]), .in7(multiplexer_1_out[7]), .in8(multiplexer_1_out[8]),
    .in9(multiplexer_1_out[9]), .in10(multiplexer_1_out[10]), .in11(multiplexer_1_out[11]),
    .in12(multiplexer_1_out[12]), .in13(multiplexer_1_out[13]), .in14(multiplexer_1_out[14]),
    .in15(multiplexer_1_out[15]), .in16(multiplexer_1_out[16]), .in17(multiplexer_1_out[17]),
    .in18(multiplexer_1_out[18]), .in19(multiplexer_1_out[19]), .in20(multiplexer_1_out[20]),
    .in21(multiplexer_1_out[21]), .in22(multiplexer_1_out[22]), .in23(multiplexer_1_out[23]),
    .in24(multiplexer_1_out[24]), .in25(multiplexer_1_out[25]), .in26(multiplexer_1_out[26]),
    .in27(multiplexer_1_out[27]), .in28(multiplexer_1_out[28]), .in29(multiplexer_1_out[29]),
    .in30(multiplexer_1_out[30]), .in31(multiplexer_1_out[31]), .num(priorityencoder_1_num),
    .any(priorityencoder_1_any));
  BarrelShifter #(.Bits(64), .direction("right")) barrelshifter_1 (
    .in({multiplexer_1_out, {32{1'b0}}}), .shift({2'b00, priorityencoder_1_num}), .out(barrelshifter_1_out));
  or or_1 (or_1_out, barrelshifter_1_out[6], barrelshifter_1_out[5], barrelshifter_1_out[4], barrelshifter_1_out[3], barrelshifter_1_out[2], barrelshifter_1_out[1], barrelshifter_1_out[0]);
  or or_2 (or_2_out, or_1_out, barrelshifter_1_out[7], barrelshifter_1_out[9]);
  and and_1 (and_1_out, or_2_out, barrelshifter_1_out[8]);
  Add #(.Bits(23)) add_2 (.a(barrelshifter_1_out[31:9]), .b({23{1'b0}}), .c_i(1'b1), .s(add_2_s));  // open: c_o
  Add #(.Bits(8)) add_3 (.a({3'b000, priorityencoder_1_num}), .b(8'h7f), .c_i(1'b0), .s(add_3_s));  // open: c_o
  Multiplexer #(.Bits(23)) multiplexer_2 (
    .sel(and_1_out), .in_0(barrelshifter_1_out[31:9]), .in_1(add_2_s), .out(f[22:0]));
  Multiplexer #(.Bits(8)) multiplexer_3 (.sel(priorityencoder_1_any), .in_0({8{1'b0}}), .in_1(add_3_s), .out(f[30:23]));

  assign f[31] = L[31];
endmodule
