// Digital circuit moduletest.dig as structural Verilog
module moduletest (
  input  in_1,
  input  in_2,
  input  [1:0] in_3,
  input  [18:0] in_4,
  input  [31:0] in_5,
  input  [18:0] in_6,
  output [7:0] out_7,
  output [7:0] out_8,
  output [7:0] out_9,
  output [7:0] out_10,
  output [7:0] out_11,
  output [7:0] out_12,
  output [7:0] out_13,
  output [7:0] out_14
);

  Byte_RAM #(.applicationType("GHDL"), .CodeFile("C:\\Users\\Gfla\\Documents\\GitHub\\RV32I\\RV32I\\Byte_RAM.vhd")) u_Byte_RAM (
    .WE(in_1), .C(in_2), .mode(in_3), .A(in_4), .Din(in_5), .A2(in_6), .D({out_14, out_13, out_12, out_11}),
    .D2({out_10, out_9, out_8, out_7}));

  // Notes on the sheet:
  //   in_6: default 12
endmodule
