// Digital circuit plotASCII.dig as structural Verilog
module plotASCII (
  input  set,
  input  [7:0] x_0,
  input  [7:0] y_0,
  input  [7:0] ASCIIptr,
  input  CC,
  output [15:0] addr,
  output en,
  output gen
);

  wire and_2_out, and_4_out, and_5_out, and_6_out, multiplexer_1_out, zero;
  wire [2:0] xASCII;
  wire [3:0] yASCII;
  wire [5:0] charROM_d;
  wire [6:0] counter_1_out;
  wire [7:0] add_2_s, add_3_s, multiplexer_4_out, multiplexer_5_out, register_1_q, register_2_q;
  wire [10:0] add_1_s, mul_1_mul;
  wire [15:11] mul_1_mul_2;

  Mul #(.Bits(8)) mul_1 (.a(8'hc), .b(ASCIIptr), .mul({mul_1_mul_2, mul_1_mul}));
  Add #(.Bits(11)) add_1 (.a(mul_1_mul), .b({{7{1'b0}}, yASCII}), .c_i(1'b0), .s(add_1_s));  // open: c_o
  ROM #(.AddrBits(11), .Bits(6)) charROM (.A(add_1_s), .sel(1'b1), .D(charROM_d));
  Multiplexer #(.Selector_Bits(3)) multiplexer_1 (
    .sel(xASCII), .in_0(charROM_d[5]), .in_1(charROM_d[4]), .in_2(charROM_d[3]), .in_3(charROM_d[2]),
    .in_4(charROM_d[1]), .in_5(charROM_d[0]), .in_6(1'b0), .in_7(1'b0), .out(multiplexer_1_out));
  RS_FF rs_ff_1 (.S(set), .C(CC), .R(and_2_out), .Q(en));
  and and_1 (gen, multiplexer_1_out, en);
  and and_2 (and_2_out, and_4_out, en);
  Counter #(.Bits(7)) counter_1 (.en(en), .C(CC), .clr(and_4_out), .out(counter_1_out));  // open: ovf
  and and_3 (zero, ~counter_1_out[6], ~counter_1_out[5], ~counter_1_out[4], ~counter_1_out[3], ~counter_1_out[2], ~counter_1_out[1], ~counter_1_out[0]);  // And
  and and_4 (and_4_out, counter_1_out[0], counter_1_out[1], counter_1_out[2], ~counter_1_out[3], ~counter_1_out[4], ~counter_1_out[5], counter_1_out[6]);  // And
  Register #(.Bits(8)) register_1 (.D(multiplexer_4_out), .C(CC), .en(en), .Q(register_1_q));
  Register #(.Bits(8)) register_2 (.D(multiplexer_5_out), .C(CC), .en(en), .Q(register_2_q));
  Multiplexer #(.Bits(8)) multiplexer_2 (.sel(zero), .in_0(register_1_q), .in_1(x_0), .out(addr[7:0]));
  Multiplexer #(.Bits(8)) multiplexer_3 (.sel(zero), .in_0(register_2_q), .in_1(y_0), .out(addr[15:8]));
  // Probe on addr[7:0]
  Add #(.Bits(8)) add_2 (.a(addr[7:0]), .b({8{1'b0}}), .c_i(1'b1), .s(add_2_s));  // open: c_o
  Add #(.Bits(8)) add_3 (.a(addr[15:8]), .b({8{1'b0}}), .c_i(1'b1), .s(add_3_s));  // open: c_o
  // Probe on add_2_s
  // Probe on addr[15:8]
  // Probe on add_3_s
  Multiplexer #(.Bits(8)) multiplexer_4 (.sel(and_5_out), .in_0(add_2_s), .in_1(x_0), .out(multiplexer_4_out));
  Multiplexer #(.Bits(8)) multiplexer_5 (.sel(and_5_out), .in_0(addr[15:8]), .in_1(add_3_s), .out(multiplexer_5_out));
  Counter #(.Bits(3)) counter_2 (.en(en), .C(CC), .clr(and_5_out), .out(xASCII));  // open: ovf
  Counter #(.Bits(4)) counter_3 (.en(and_5_out), .C(CC), .clr(and_6_out), .out(yASCII));  // open: ovf
  and and_5 (and_5_out, xASCII[0], ~xASCII[1], xASCII[2]);  // And
  and and_6 (and_6_out, ~yASCII[0], ~yASCII[1], yASCII[2], yASCII[3]);  // And

  // Other names for the same wires on the sheet: x[7:0] = addr[7:0]; y[7:0] = addr[15:8]

  // Notes on the sheet:
  //   CC: Hz: 10
  //   contents of charROM (hex, n*v repeats v):
  //   397*0,6*8,0,0,8,0,0,4*14,9*0,14,14,3e,14,14,14,3e,14,14,0,0,0
  //   ,8,1e,28,28,1c,a,a,3c,8,0,0,0,10,28,12,4,8,10,24,a,4,0,0,0,18
  //   ,24,24,18,12,2a,24,24,1a,0,0,4*8,8*0,4,8,8,5*10,8,8,4,0,10,8,8
  //   ,5*4,8,8,10,0,0,0,8,2a,1c,8,1c,2a,8,6*0,8,8,3e,8,8,11*0,8,1c,8
  //   ,10,6*0,3e,13*0,8,1c,8,0,0,0,2,2,4,4,8,8,10,10,20,20,0,0,1c,22,22
  //   ,26,2a,32,22,22,1c,0,0,0,8,18,28,6*8,0,0,0,1c,22,22,2,4,8,10,20
  //   ,3e,0,0,0,3e,2,4,8,1c,2,2,22,1c,0,0,0,c,c,14,14,24,24,3e,4,4,0,0,0
  //   ,3e,20,20,3c,2,2,22,22,1c,0,0,0,c,10,20,3c,4*22,1c,0,0,0,3e,2
  //   ,4,4,8,8,10,10,10,0,0,0,1c,22,22,14,8,14,22,22,1c,0,0,0,1c,4*22
  //   ,1e,2,4,18,5*0,8,1c,8,0,8,1c,8,5*0,8,1c,8,0,8,1c,8,10,0,0,2,4
  //   ,8,10,20,10,8,4,2,6*0,3e,0,3e,6*0,20,10,8,4,2,4,8,10,20,0,0,0
  //   ,1c,22,22,2,4,8,8,0,8,0,0,0,1c,22,2e,2a,2a,2a,2e,20,1c,0,0,0,8,8
  //   ,14,14,14,3e,22,22,22,0,0,0,3c,22,22,22,3c,22,22,22,3c,0,0,0,1c
  //   ,22,5*20,22,1c,0,0,0,38,24,5*22,24,38,0,0,0,3e,20,20,20,3c,20,20,20
  //   ,3e,0,0,0,3e,20,20,20,3c,4*20,0,0,0,1c,22,20,20,2e,22,22,22,1e
  //   ,0,0,0,4*22,3e,4*22,0,0,0,1c,7*8,1c,0,0,0,5*2,22,22,22,1c,0,0,0
  //   ,22,24,28,30,30,28,24,22,22,0,0,0,8*20,3e,0,0,0,22,36,2a,6*22
  //   ,0,0,0,22,32,2a,26,5*22,0,0,0,1c,7*22,1c,0,0,0,3c,22,22,22,3c
  //   ,4*20,0,0,0,1c,7*22,1c,4,3,0,3c,22,22,22,3c,28,24,22,22,0,0,0
  //   ,1c,22,20,20,1c,2,2,22,1c,0,0,0,3e,8*8,0,0,0,8*22,1c,0,0,0,4*22
  //   ,14,14,14,8,8,0,0,0,6*2a,14,14,14,0,0,0,22,22,14,14,8,14,14,22,22
  //   ,0,0,0,22,22,14,14,5*8,0,0,0,3e,2,4,4,8,10,10,20,3e,0,0,1c,9*10
  //   ,1c,0,0,20,20,10,10,8,8,4,4,2,2,0,1c,9*4,1c,0,8,14,22,19*0,3e
  //   ,0,10,10,8,8,12*0,1c,2,1e,22,22,1e,0,0,0,20,20,20,3c,4*22,3c,6*0
  //   ,1c,22,20,20,22,1c,0,0,0,2,2,2,1e,4*22,1e,6*0,1c,22,3e,20,22,1c
  //   ,0,0,0,6,8,8,8,3e,4*8,6*0,1e,22,22,22,1e,2,22,1c,0,20,20,20,2c
  //   ,32,4*22,0,0,8,0,0,0,18,4*8,1c,0,0,4,0,0,0,c,6*4,38,0,20,20,20
  //   ,24,28,30,28,24,22,0,0,0,18,7*8,c,6*0,3c,5*2a,6*0,2c,32,4*22,6*0
  //   ,1c,4*22,1c,6*0,3c,22,22,22,3c,20,20,20,4*0,1e,22,22,22,1e,2,2,2
  //   ,4*0,2c,32,4*20,6*0,1c,22,3c,2,22,1c,0,0,0,10,10,10,3c,10,10,10
  //   ,12,c,6*0,4*22,26,1a,6*0,22,22,14,14,8,8,6*0,4*2a,14,14,6*0,22
  //   ,14,8,8,14,22,6*0,4*22,1e,2,22,1c,4*0,3e,4,8,10,20,3e,0,0,6,4*8
  //   ,30,4*8,6,0,11*8,0,30,4*8,6,4*8,30,0,0,1a,2c
endmodule
