// Digital circuit plotLine.dig as structural Verilog
module plotLine (
  input  set,
  input  [8:0] dx,
  input  [8:0] dy,
  input  [7:0] x_0,
  input  [7:0] y_0,
  input  CC,
  output [15:0] addr,
  output en
);

  wire comparator_1_lt, comparator_2_lt, comparator_3_eq, comparator_4_lt, comparator_5_eq, comparator_5_gt,
       en_t, or_2_out, zero;
  wire [7:0] counter_1_out;
  wire [8:0] add_1_s, add_3_s, add_4_s, add_7_s, add_8_s, add_10_s, add_11_s, ax, ay, bx, by, d, dx_plus,
       dy_plus, ix, iy, multiplexer_2_out, multiplexer_15_out, multiplexer_16_out, not_1_out, not_2_out,
       not_3_out, register_2_q, register_3_q;
  wire [8:8] xx, yy;
  wire [9:0] a, add_6_s, add_9_s, b, e, multiplexer_9_out, multiplexer_14_out, register_1_q;

  RS_FF rs_ff_1 (.S(set), .C(CC), .R(comparator_3_eq), .Q(en_t));
  assign not_1_out = ~dx;  // Not not_1, 9 bits wide
  Comparator #(.Signed("true"), .Bits(9)) comparator_1 (
    .a(dx_plus), .b(dy_plus), .lt(comparator_1_lt));  // open: gt, eq
  Add #(.Bits(9)) add_1 (.a(not_1_out), .b({9{1'b0}}), .c_i(1'b1), .s(add_1_s));  // open: c_o
  or or_1 (en, set, en_t);
  Multiplexer #(.Bits(9)) multiplexer_1 (.sel(comparator_1_lt), .in_0(dx_plus), .in_1(dy_plus), .out(d));
  Multiplexer #(.Bits(9)) multiplexer_2 (
    .sel(comparator_1_lt), .in_0(dy_plus), .in_1(dx_plus), .out(multiplexer_2_out));
  Counter #(.Bits(8)) counter_1 (.en(en_t), .C(CC), .clr(comparator_3_eq), .out(counter_1_out));  // open: ovf
  Multiplexer #(.Bits(9)) multiplexer_3 (.sel(comparator_2_lt), .in_0(dx), .in_1(add_1_s), .out(dx_plus));
  Comparator #(.Signed("true"), .Bits(9)) comparator_2 (.a(dx), .b({9{1'b0}}), .lt(comparator_2_lt));  // open: gt, eq
  Multiplexer #(.Bits(9)) multiplexer_4 (.sel(comparator_1_lt), .in_0(ix), .in_1({9{1'b0}}), .out(ax));
  Add #(.Bits(10)) add_2 (
    .a({1'b0, multiplexer_2_out}), .b({1'b0, multiplexer_2_out}), .c_i(1'b0), .s(a));  // open: c_o
  // Probe on counter_1_out
  Multiplexer #(.Bits(9)) multiplexer_5 (.sel(comparator_2_lt), .in_0(9'h1), .in_1({9{1'b1}}), .out(ix));
  Multiplexer #(.Bits(9)) multiplexer_6 (.sel(comparator_1_lt), .in_0({9{1'b0}}), .in_1(iy), .out(ay));
  Comparator #(.Bits(8)) comparator_3 (.a(counter_1_out), .b(d[7:0]), .eq(comparator_3_eq));  // open: gt, lt
  Multiplexer #(.Bits(9)) multiplexer_7 (.sel(comparator_1_lt), .in_0({9{1'b0}}), .in_1(ix), .out(bx));
  and and_1 (zero, ~counter_1_out[7], ~counter_1_out[6], ~counter_1_out[5], ~counter_1_out[4], ~counter_1_out[3], ~counter_1_out[2], ~counter_1_out[1], ~counter_1_out[0]);  // And
  assign not_2_out = ~dy;  // Not not_2, 9 bits wide
  assign not_3_out = ~d;  // Not not_3, 9 bits wide
  Add #(.Bits(9)) add_3 (.a(not_3_out), .b({9{1'b0}}), .c_i(1'b1), .s(add_3_s));  // open: c_o
  Add #(.Bits(9)) add_4 (.a(not_2_out), .b({9{1'b0}}), .c_i(1'b1), .s(add_4_s));  // open: c_o
  Multiplexer #(.Bits(9)) multiplexer_8 (.sel(comparator_1_lt), .in_0(iy), .in_1({9{1'b0}}), .out(by));
  BitExtender #(.inputBits(9), .outputBits(10)) bitextender_1 (.in(add_3_s), .out(e));
  Register #(.Bits(10)) register_1 (.D(multiplexer_14_out), .C(CC), .en(en_t), .Q(register_1_q));
  Register #(.Bits(9)) register_2 (.D(multiplexer_15_out), .C(CC), .en(en_t), .Q(register_2_q));
  Register #(.Bits(9)) register_3 (.D(multiplexer_16_out), .C(CC), .en(en_t), .Q(register_3_q));
  Multiplexer #(.Bits(10)) multiplexer_9 (.sel(zero), .in_0(register_1_q), .in_1(e), .out(multiplexer_9_out));
  Multiplexer #(.Bits(9)) multiplexer_10 (
    .sel(zero), .in_0(register_2_q), .in_1({1'b0, x_0}), .out({xx[8], addr[7:0]}));
  Multiplexer #(.Bits(9)) multiplexer_11 (
    .sel(zero), .in_0(register_3_q), .in_1({1'b0, y_0}), .out({yy[8], addr[15:8]}));
  Multiplexer #(.Bits(9)) multiplexer_12 (.sel(comparator_4_lt), .in_0(dy), .in_1(add_4_s), .out(dy_plus));
  Add #(.Bits(10)) add_5 (.a(e), .b(e), .c_i(1'b0), .s(b));  // open: c_o
  // Probe on multiplexer_9_out
  // Probe on a
  // Probe on ax
  // Probe on ay
  Multiplexer #(.Bits(9)) multiplexer_13 (.sel(comparator_4_lt), .in_0(9'h1), .in_1({9{1'b1}}), .out(iy));
  Comparator #(.Signed("true"), .Bits(9)) comparator_4 (.a(dy), .b({9{1'b0}}), .lt(comparator_4_lt));  // open: gt, eq
  Add #(.Bits(10)) add_6 (.a(multiplexer_9_out), .b(a), .c_i(1'b0), .s(add_6_s));  // open: c_o
  Add #(.Bits(9)) add_7 (.a({xx[8], addr[7:0]}), .b(ax), .c_i(1'b0), .s(add_7_s));  // open: c_o
  Add #(.Bits(9)) add_8 (.a({yy[8], addr[15:8]}), .b(ay), .c_i(1'b0), .s(add_8_s));  // open: c_o
  // Probe on b
  // Probe on bx
  // Probe on by
  Add #(.Bits(10)) add_9 (.a(add_6_s), .b(b), .c_i(1'b0), .s(add_9_s));  // open: c_o
  Add #(.Bits(9)) add_10 (.a(add_7_s), .b(bx), .c_i(1'b0), .s(add_10_s));  // open: c_o
  Add #(.Bits(9)) add_11 (.a(add_8_s), .b(by), .c_i(1'b0), .s(add_11_s));  // open: c_o
  Multiplexer #(.Bits(10)) multiplexer_14 (.sel(or_2_out), .in_0(add_6_s), .in_1(add_9_s), .out(multiplexer_14_out));
  Multiplexer #(.Bits(9)) multiplexer_15 (.sel(or_2_out), .in_0(add_7_s), .in_1(add_10_s), .out(multiplexer_15_out));
  Multiplexer #(.Bits(9)) multiplexer_16 (.sel(or_2_out), .in_0(add_8_s), .in_1(add_11_s), .out(multiplexer_16_out));
  Comparator #(.Signed("true"), .Bits(10)) comparator_5 (
    .a(add_6_s), .b({10{1'b0}}), .gt(comparator_5_gt), .eq(comparator_5_eq));  // open: lt
  or or_2 (or_2_out, comparator_5_gt, comparator_5_eq);

  // Other names for the same wires on the sheet: xx[7:0] = addr[7:0]; yy[7:0] = addr[15:8]

  // Notes on the sheet:
  //   CC: Hz: 2
  //   Bresenham Algorithm
endmodule
