// Digital circuit plotRect.dig as structural Verilog
module plotRect (
  input  set,
  input  [8:0] dx,
  input  [8:0] dy,
  input  [7:0] x_0,
  input  [7:0] y_0,
  input  [7:0] x_1,
  input  CC,
  output [15:0] addr,
  output en
);

  wire and_1_out, comparator_1_eq, comparator_1_gt, comparator_2_eq, comparator_2_gt, comparator_3_eq,
       comparator_4_eq, or_1_out, or_2_out, zero;
  wire [7:0] add_5_s, add_6_s, multiplexer_7_out, multiplexer_8_out, register_1_q, register_2_q, xx, yy;
  wire [8:0] add_1_s, add_2_s, add_3_s, add_4_s, multiplexer_2_out, multiplexer_3_out, not_1_out, not_2_out;
  wire [15:0] counter_1_out, d;
  wire [17:0] mul_1_mul;
  wire [17:16] sub_1_s;

  RS_FF rs_ff_1 (.S(set), .C(CC), .R(and_1_out), .Q(en));
  and and_1 (and_1_out, comparator_3_eq, en);
  assign not_1_out = ~dx;  // Not not_1, 9 bits wide
  assign not_2_out = ~dy;  // Not not_2, 9 bits wide
  Counter #(.Bits(16)) counter_1 (.en(en), .C(CC), .clr(comparator_3_eq), .out(counter_1_out));  // open: ovf
  Comparator #(.Signed("true"), .Bits(9)) comparator_1 (
    .a(dx), .b({9{1'b0}}), .gt(comparator_1_gt), .eq(comparator_1_eq));  // open: lt
  Add #(.Bits(9)) add_1 (.a(not_1_out), .b({9{1'b0}}), .c_i(1'b1), .s(add_1_s));  // open: c_o
  Add #(.Bits(9)) add_2 (.a(not_2_out), .b({9{1'b0}}), .c_i(1'b1), .s(add_2_s));  // open: c_o
  Comparator #(.Signed("true"), .Bits(9)) comparator_2 (
    .a(dy), .b({9{1'b0}}), .gt(comparator_2_gt), .eq(comparator_2_eq));  // open: lt
  // Probe on counter_1_out
  Multiplexer #(.Bits(8)) multiplexer_1 (.sel(or_1_out), .in_0({8{1'b1}}), .in_1(8'h1), .out(xx));
  or or_1 (or_1_out, comparator_1_gt, comparator_1_eq);
  Multiplexer #(.Bits(9)) multiplexer_2 (.sel(or_1_out), .in_0(add_1_s), .in_1(dx), .out(multiplexer_2_out));
  Multiplexer #(.Bits(9)) multiplexer_3 (.sel(or_2_out), .in_0(add_2_s), .in_1(dy), .out(multiplexer_3_out));
  or or_2 (or_2_out, comparator_2_gt, comparator_2_eq);
  Multiplexer #(.Bits(8)) multiplexer_4 (.sel(or_2_out), .in_0({8{1'b1}}), .in_1(8'h1), .out(yy));
  Comparator #(.Bits(16)) comparator_3 (.a(counter_1_out), .b(d), .eq(comparator_3_eq));  // open: gt, lt
  and and_2 (zero, ~counter_1_out[15], ~counter_1_out[14], ~counter_1_out[13], ~counter_1_out[12], ~counter_1_out[11], ~counter_1_out[10], ~counter_1_out[9], ~counter_1_out[8], ~counter_1_out[7], ~counter_1_out[6], ~counter_1_out[5], ~counter_1_out[4], ~counter_1_out[3], ~counter_1_out[2], ~counter_1_out[1], ~counter_1_out[0]);  // And
  Add #(.Bits(9)) add_3 (.a(multiplexer_2_out), .b({9{1'b0}}), .c_i(1'b1), .s(add_3_s));  // open: c_o
  Add #(.Bits(9)) add_4 (.a({9{1'b0}}), .b(multiplexer_3_out), .c_i(1'b1), .s(add_4_s));  // open: c_o
  // Probe on add_3_s
  Mul #(.Bits(9)) mul_1 (.a(add_3_s), .b(add_4_s), .mul(mul_1_mul));
  // Probe on add_4_s
  Register #(.Bits(8)) register_1 (.D(multiplexer_7_out), .C(CC), .en(en), .Q(register_1_q));
  Register #(.Bits(8)) register_2 (.D(multiplexer_8_out), .C(CC), .en(en), .Q(register_2_q));
  Sub #(.Bits(18)) sub_1 (.a(mul_1_mul), .b({18{1'b0}}), .c_i(1'b1), .s({sub_1_s, d}));  // open: c_o
  Multiplexer #(.Bits(8)) multiplexer_5 (.sel(zero), .in_0(register_1_q), .in_1(x_0), .out(addr[7:0]));
  Multiplexer #(.Bits(8)) multiplexer_6 (.sel(zero), .in_0(register_2_q), .in_1(y_0), .out(addr[15:8]));
  // Probe on {sub_1_s, d}
  // Probe on addr[7:0]
  Add #(.Bits(8)) add_5 (.a(addr[7:0]), .b(xx), .c_i(1'b0), .s(add_5_s));  // open: c_o
  // Probe on addr[15:8]
  Add #(.Bits(8)) add_6 (.a(addr[15:8]), .b(yy), .c_i(1'b0), .s(add_6_s));  // open: c_o
  // Probe on add_5_s
  Multiplexer #(.Bits(8)) multiplexer_7 (.sel(comparator_4_eq), .in_0(add_5_s), .in_1(x_0), .out(multiplexer_7_out));
  Multiplexer #(.Bits(8)) multiplexer_8 (
    .sel(comparator_4_eq), .in_0(addr[15:8]), .in_1(add_6_s), .out(multiplexer_8_out));
  // Probe on add_6_s
  Comparator #(.Bits(8)) comparator_4 (.a(addr[7:0]), .b(x_1), .eq(comparator_4_eq));  // open: gt, lt

  // Other names for the same wires on the sheet: x[7:0] = addr[7:0]; y[7:0] = addr[15:8]

  // Notes on the sheet:
  //   CC: Hz: 10
endmodule
