// Digital circuit top.dig as structural Verilog
module top (
  input  clk,
  output [31:0] out_1,
  output [31:0] out_2,
  output [31:0] out_3,
  output [31:0] PC,
  output [31:0] out_5,
  output [31:0] out_6,
  output [31:0] out_7,
  output [31:0] out_8,
  output [31:0] out_9,
  output [6:0] out_10
);

  wire addressdecorder_1_gcen, addressdecorder_1_gpuen, addressdecorder_1_ramen, AddressSrc, ALUSrc,
       and_1_out, and_2_out, button_1_out, C, dipswitch_1_out, ExeSrc, floatRegWrite, FPUCtrl, FPUSrc,
       instr_decorder_1_p2, instr_decorder_1_p3, JumpSrc, MemSrc, MemWrite, or_1_out, RegWrite, zero;
  wire [1:0] ResultSrc;
  wire [2:0] funct3, ImmSrc;
  wire [3:0] counter_1_out;
  wire [4:0] ALUCtrl, instr_decorder_1_p18, instr_decorder_1_p19, instr_decorder_1_p20;
  wire [23:0] _2A, addressdecorder_1_a_share;
  wire [24:0] instr_decorder_1_p21;
  wire [31:0] _1P, _2D, add_1_s, add_2_s, addressdecorder_1_d, ALU, bD, extender_1_extended,
       floatreg_file_1_fs1, floatreg_file_1_fs2, fpu_1_p4, gamecontrollerio_1_d, gpu_1_d, mergedata_1_rd,
       multiplexer_1_out, multiplexer_3_out, multiplexer_4_out, multiplexer_5_out, multiplexer_6_out,
       multiplexer_7_out, multiplexer_8_out, multiplexer_9_out, ramdualaccess_1_d1, reg_file_1_rs1,
       reg_file_1_rs2, rom_1_d;

  Multiplexer #(.Bits(32)) multiplexer_1 (
    .sel(or_1_out), .in_0(add_1_s), .in_1(multiplexer_9_out), .out(multiplexer_1_out));
  Counter #(.Bits(4)) counter_1 (.en(1'b1), .C(clk), .clr(1'b0), .out(counter_1_out));  // open: ovf
  D_FF #(.Bits(24)) d_ff_1 (.D(multiplexer_1_out[23:0]), .C(C), .Q(PC[23:0]));  // open: nQ
  ROM #(.AddrBits(24), .isProgramMemory("true"), .Bits(32)) rom_1 (.A(PC[23:0]), .sel(1'b1), .D(rom_1_d));
  Add #(.Bits(32)) add_1 (.a({{8{1'b0}}, PC[23:0]}), .b({32{1'b0}}), .c_i(1'b1), .s(add_1_s));  // open: c_o
  DipSwitch dipswitch_1 (.out(dipswitch_1_out));
  Multiplexer multiplexer_2 (.sel(dipswitch_1_out), .in_0(counter_1_out[3]), .in_1(button_1_out), .out(C));
  Button button_1 (.out(button_1_out));
  // Instr_Decorder instr_decorder_1: pin names not known; wires that end beside it: rom_1_d, instr_decorder_1_p2, instr_decorder_1_p3, AddressSrc, MemSrc, ExeSrc, floatRegWrite, FPUSrc, FPUCtrl, ALUCtrl, RegWrite, ImmSrc, ALUSrc, ResultSrc, JumpSrc, MemWrite, funct3, instr_decorder_1_p18, instr_decorder_1_p19, instr_decorder_1_p20, instr_decorder_1_p21
  or or_1 (or_1_out, instr_decorder_1_p2, and_1_out);
  and and_1 (and_1_out, instr_decorder_1_p3, zero);
  REG_FILE reg_file_1 (
    .WE(RegWrite), .A_rs1(instr_decorder_1_p18), .A_rs2(instr_decorder_1_p19), .A_rd(instr_decorder_1_p20),
    .WD(multiplexer_8_out), .C(C), .rs1(reg_file_1_rs1), .rs2(reg_file_1_rs2), .a_0(out_1), .a_1(out_2),
    .a_2(out_3), .t_0(out_5));
  FloatREG_FILE floatreg_file_1 (
    .WE(floatRegWrite), .WD(multiplexer_8_out), .A_fs1(instr_decorder_1_p18), .A_fs2(instr_decorder_1_p19),
    .A_fd(instr_decorder_1_p20), .C(C), .fs1(floatreg_file_1_fs1), .fs2(floatreg_file_1_fs2), .fa_0(out_6),
    .Q_11(out_7), .Q_12(out_8), .Q_13(out_9));
  Extender extender_1 (.src(ImmSrc), .Imm(instr_decorder_1_p21), .Extended(extender_1_extended));
  Multiplexer #(.Bits(32)) multiplexer_3 (.sel(AddressSrc), .in_0(reg_file_1_rs1), .in_1(ALU), .out(multiplexer_3_out));
  Multiplexer #(.Bits(32)) multiplexer_4 (
    .sel(MemSrc), .in_0(reg_file_1_rs2), .in_1(floatreg_file_1_fs2), .out(multiplexer_4_out));
  Button button_2 (.out(_1P[18]));
  AddressDecorder addressdecorder_1 (
    .A(multiplexer_3_out), .WD(multiplexer_4_out), .Imm(extender_1_extended), .funct3(funct3), .bD(bD),
    .MemWrite(MemWrite), .GPUen(addressdecorder_1_gpuen), .A_share(addressdecorder_1_a_share),
    .D(addressdecorder_1_d), .GCen(addressdecorder_1_gcen), .RAMen(addressdecorder_1_ramen));
  Button button_3 (.out(_1P[10]));
  Button button_4 (.out(_1P[8]));
  Button button_5 (.out(_1P[2]));
  Button button_6 (.out(_1P[3]));
  Button button_7 (.out(_1P[1]));
  Button button_8 (.out(_1P[12]));
  Button button_9 (.out(_1P[19]));
  Button button_10 (.out(_1P[17]));
  Button button_11 (.out(_1P[16]));
  Button button_12 (.out(_1P[28]));
  Multiplexer #(.Bits(32)) multiplexer_5 (
    .sel(ALUSrc), .in_0(reg_file_1_rs2), .in_1(extender_1_extended), .out(multiplexer_5_out));
  Multiplexer #(.Bits(32)) multiplexer_6 (
    .sel(FPUSrc), .in_0(floatreg_file_1_fs1), .in_1(reg_file_1_rs1), .out(multiplexer_6_out));
  Add #(.Bits(32)) add_2 (.a({{8{1'b0}}, PC[23:0]}), .b(extender_1_extended), .c_i(1'b0), .s(add_2_s));  // open: c_o
  Button button_13 (.out(_1P[0]));
  Button button_14 (.out(_1P[13]));
  Button button_15 (.out(_1P[14]));
  Button button_16 (.out(_1P[15]));
  Button button_17 (.out(_1P[31]));
  and and_2 (and_2_out, addressdecorder_1_ramen, MemWrite);
  ALU alu_1 (.Ctrl(ALUCtrl), .s1(reg_file_1_rs1), .s2(multiplexer_5_out), .zero(zero), .result(ALU));
  // FPU fpu_1: pin names not known; wires that end beside it: FPUCtrl, multiplexer_6_out, floatreg_file_1_fs2, fpu_1_p4
  Button button_18 (.out(_1P[26]));
  GPU gpu_1 (
    .CC(clk), .C(C), .Din(addressdecorder_1_d), .WE(MemWrite), .A(addressdecorder_1_a_share),
    .en(addressdecorder_1_gpuen), .D(gpu_1_d), .col(out_10));
  GameControllerIO gamecontrollerio_1 (
    ._1P(_1P), ._2P({32{1'b0}}), ._3P({32{1'b0}}), ._4P({32{1'b0}}), .C(C), .WE(MemWrite),
    .A(addressdecorder_1_a_share), .Din(addressdecorder_1_d), .en(addressdecorder_1_gcen),
    .D(gamecontrollerio_1_d));
  RAMDualAccess #(.AddrBits(24), .Bits(32)) ramdualaccess_1 (
    .str(and_2_out), .C(C), .ld(1'b1), .A1(addressdecorder_1_a_share), .Din1(addressdecorder_1_d), .A2(_2A),
    .D1(ramdualaccess_1_d1), .D2(_2D));
  Button button_19 (.out(_1P[11]));
  Button button_20 (.out(_1P[9]));
  Button button_21 (.out(_1P[6]));
  Button button_22 (.out(_1P[7]));
  Button button_23 (.out(_1P[5]));
  Button button_24 (.out(_1P[20]));
  Button button_25 (.out(_1P[27]));
  Button button_26 (.out(_1P[25]));
  Button button_27 (.out(_1P[24]));
  Button button_28 (.out(_1P[29]));
  Button button_29 (.out(_1P[30]));
  Multiplexer #(.Bits(32)) multiplexer_7 (.sel(ExeSrc), .in_0(ALU), .in_1(fpu_1_p4), .out(multiplexer_7_out));
  Button button_30 (.out(_1P[4]));
  Button button_31 (.out(_1P[21]));
  Button button_32 (.out(_1P[22]));
  Button button_33 (.out(_1P[23]));
  assign bD = addressdecorder_1_gpuen ? gpu_1_d : 32'bz;  // Driver driver_1
  assign bD = addressdecorder_1_gcen ? gamecontrollerio_1_d : 32'bz;  // Driver driver_2
  assign bD = addressdecorder_1_ramen ? ramdualaccess_1_d1 : 32'bz;  // Driver driver_3
  MergeData mergedata_1 (.D(bD), .imm(extender_1_extended), .funct3(funct3), .RD(mergedata_1_rd));
  RAMViewer ramviewer_1 (.CC(clk), ._2D(_2D), ._2A(_2A));
  Multiplexer #(.Selector_Bits(2), .Bits(32)) multiplexer_8 (
    .sel(ResultSrc), .in_0(mergedata_1_rd), .in_1(multiplexer_7_out), .in_2(add_1_s), .in_3(add_2_s),
    .out(multiplexer_8_out));
  Multiplexer #(.Bits(32)) multiplexer_9 (
    .sel(JumpSrc), .in_0(multiplexer_7_out), .in_1(add_2_s), .out(multiplexer_9_out));

  assign PC[31:24] = {8{1'b0}};

  // Other names for the same wires on the sheet: a_0[31:0] = out_1; A_1 = _1P[4]; a_4[31:0] = out_2; B_1 = _1P[5];
  //   CC = clk; DOWN_1 = _1P[1]; fa_0[31:0] = out_6; L1_1 = _1P[8]; L2_1 = _1P[10]; L3_1 = _1P[28]; LE_1 = _1P[14];
  //   LEFT_1 = _1P[3]; LN_1 = _1P[12]; LNE_1 = _1P[13]; LNW_1 = _1P[19]; LS_1 = _1P[16]; LSE_1 = _1P[15];
  //   LSW_1 = _1P[17]; LW_1 = _1P[18]; Q_11[31:0] = out_7; Q_12[31:0] = out_8; Q_13[31:0] = out_9; R1_1 = _1P[9];
  //   R2_1 = _1P[11]; R3_1 = _1P[29]; RE_1 = _1P[22]; RIGHT_1 = _1P[0]; RN_1 = _1P[20]; RNE_1 = _1P[21];
  //   RNW_1 = _1P[27]; RS_1 = _1P[24]; RSE_1 = _1P[23]; RSW_1 = _1P[25]; RW_1 = _1P[26]; SELECT_1 = _1P[31];
  //   START_1 = _1P[30]; t_0[31:0] = out_5; t_2[31:0] = out_3; UP_1 = _1P[2]; X_1 = _1P[6]; Y_1 = _1P[7]

  // Notes on the sheet:
  //   clk: Hz: 2147483647
  //   rom_1 loads out.hex
endmodule
