// Digital circuit top2.dig as structural Verilog
module top2 (
  input  clk,
  output [31:0] out_1,
  output [31:0] out_2,
  output [31:0] out_3,
  output [31:0] PC,
  output [31:0] out_5,
  output [31:0] out_6,
  output [31:0] out_7,
  output [31:0] out_8,
  output [31:0] out_9,
  output [6:0] col
);

  wire addressdecorder_1_p6, addressdecorder_1_p7, ALUSrc, and_1_out, and_5_out, Apos_0, ASCIIptr_0,
       ASCIIptr_1, b, button_1_out, C, dipswitch_1_out, en, exe, ExeSrc, floatRegWrite, FPUCtrl, FPUSrc, h,
       instr_decorder_1_p2, instr_decorder_1_p3, JumpSrc, MemSrc, MemWrite, onecolor_0, onecolor_1,
       onecolor_2, onecolor_3, or_1_out, or_2_out, or_3_out, plotASCII, plotASCII_en, plotASCII_gen,
       plotLine, plotLine_en, plotRect, plotRect_en, pos_0, pos_1, pos_2, pos_3, RegWrite, str, str_0,
       str_0_Apos_0, str_0_Apos_1, str_0_ASCIIptr_0, str_0_ASCIIptr_1, str_0_onecolor_0, str_0_onecolor_1,
       str_0_onecolor_2, str_0_onecolor_3, str_0_pos_0, str_0_pos_1, str_0_pos_2, str_0_pos_3, str_1,
       str_1_Apos_0, str_1_Apos_1, str_1_ASCIIptr_0, str_1_ASCIIptr_1, str_1_onecolor_0, str_1_onecolor_1,
       str_1_onecolor_2, str_1_onecolor_3, str_1_pos_0, str_1_pos_1, str_1_pos_2, str_1_pos_3, str_2,
       str_2_Apos_0, str_2_Apos_1, str_2_ASCIIptr_0, str_2_ASCIIptr_1, str_2_onecolor_0, str_2_onecolor_1,
       str_2_onecolor_2, str_2_onecolor_3, str_2_pos_0, str_2_pos_1, str_2_pos_2, str_2_pos_3, str_3_Apos_0,
       str_3_Apos_1, str_3_ASCIIptr_0, str_3_ASCIIptr_1, str_3_onecolor_0, str_3_onecolor_1,
       str_3_onecolor_2, str_3_onecolor_3, str_3_pos_1, str_3_pos_2, str_3_pos_3, w, zero;
  wire [0:0] Q_en;
  wire [1:0] ResultSrc;
  wire [2:0] funct3, ImmSrc;
  wire [3:0] counter_1_out;
  wire [4:0] ALUCtrl, instr_decorder_1_p17, instr_decorder_1_p18, instr_decorder_1_p19;
  wire [7:0] D_0, D_1, D_2, D_3, D_Apos_0, D_Apos_1, D_ASCIIptr_0, D_ASCIIptr_1, D_exe, D_onecolor_0,
       D_onecolor_1, D_onecolor_2, D_onecolor_3, D_pos_0, D_pos_1, D_pos_2, D_pos_3, Din_0, Din_0_D_Apos_0,
       Din_0_D_Apos_1, Din_0_D_ASCIIptr_0, Din_0_D_ASCIIptr_1, Din_0_D_onecolor_0, Din_0_D_onecolor_1,
       Din_0_D_onecolor_2, Din_0_D_onecolor_3, Din_0_D_pos_0, Din_0_D_pos_1, Din_0_D_pos_2, Din_0_D_pos_3,
       Din_1, Din_1_D_Apos_0, Din_1_D_Apos_1, Din_1_D_ASCIIptr_0, Din_1_D_ASCIIptr_1, Din_1_D_onecolor_0,
       Din_1_D_onecolor_1, Din_1_D_onecolor_2, Din_1_D_onecolor_3, Din_1_D_pos_0, Din_1_D_pos_1,
       Din_1_D_pos_2, Din_1_D_pos_3, Din_2, Din_2_D_Apos_0, Din_2_D_Apos_1, Din_2_D_ASCIIptr_0,
       Din_2_D_ASCIIptr_1, Din_2_D_onecolor_0, Din_2_D_onecolor_1, Din_2_D_onecolor_2, Din_2_D_onecolor_3,
       Din_2_D_pos_0, Din_2_D_pos_1, Din_2_D_pos_2, Din_2_D_pos_3, Din_3, Din_3_D_Apos_0, Din_3_D_Apos_1,
       Din_3_D_ASCIIptr_0, Din_3_D_ASCIIptr_1, Din_3_D_onecolor_0, Din_3_D_onecolor_1, Din_3_D_onecolor_2,
       Din_3_D_onecolor_3, Din_3_D_pos_1, Din_3_D_pos_2, Din_3_D_pos_3, Q_Apos_0, Q_Apos_1, Q_ASCIIptr0,
       Q_ASCIIptr1, Q_onecolor1, Q_onecolor2, Q_onecolor3, Q_pos0, Q_pos1, Q_pos2, Q_pos3;
  wire [7:7] Q_onecolor0;
  wire [8:0] dx, dy;
  wire [15:0] driver_1_out, plotascii_1_addr, plotline_1_addr, plotrect_1_addr;
  wire [18:0] _2A, addressdecorder_1_p4;
  wire [24:0] instr_decorder_1_p20;
  wire [31:0] _1P, _2D, add_1_s, add_2_s, ALU, driver_4_out, extender_1_extended, floatreg_file_1_fs1,
       floatreg_file_1_fs2, fpu_1_p4, gamecontrollerio_1_p8, mergedata_1_rd, multiplexer_1_out,
       multiplexer_3_out, multiplexer_4_out, multiplexer_5_out, multiplexer_6_out, multiplexer_7_out,
       multiplexer_8_out, reg_file_1_rs1, reg_file_1_rs2, rom_1_d, u_Byte_RAM_d;

  Multiplexer #(.Bits(32)) multiplexer_1 (
    .sel(or_1_out), .in_0(add_1_s), .in_1(multiplexer_8_out), .out(multiplexer_1_out));
  D_FF #(.Bits(24)) d_ff_1 (.D(multiplexer_1_out[23:0]), .C(C), .Q(PC[23:0]));  // open: nQ
  Counter #(.Bits(4)) counter_1 (.en(1'b1), .C(clk), .clr(1'b0), .out(counter_1_out));  // open: ovf
  ROM #(.AddrBits(24), .isProgramMemory("true"), .Bits(32)) rom_1 (.A(PC[23:0]), .sel(1'b1), .D(rom_1_d));
  Add #(.Bits(32)) add_1 (.a({{8{1'b0}}, PC[23:0]}), .b({32{1'b0}}), .c_i(1'b1), .s(add_1_s));  // open: c_o
  // Instr_Decorder instr_decorder_1: pin names not known; wires that end beside it: rom_1_d, instr_decorder_1_p2, instr_decorder_1_p3, MemSrc, ExeSrc, floatRegWrite, FPUSrc, FPUCtrl, ALUCtrl, RegWrite, ImmSrc, ALUSrc, ResultSrc, JumpSrc, MemWrite, funct3, instr_decorder_1_p17, instr_decorder_1_p18, instr_decorder_1_p19, instr_decorder_1_p20
  DipSwitch #(.dipDefault("true")) dipswitch_1 (.out(dipswitch_1_out));
  Multiplexer multiplexer_2 (.sel(dipswitch_1_out), .in_0(counter_1_out[0]), .in_1(button_1_out), .out(C));
  Button button_1 (.out(button_1_out));
  or or_1 (or_1_out, instr_decorder_1_p2, and_1_out);
  and and_1 (and_1_out, instr_decorder_1_p3, zero);
  REG_FILE reg_file_1 (
    .WE(RegWrite), .A_rs1(instr_decorder_1_p17), .A_rs2(instr_decorder_1_p18), .A_rd(instr_decorder_1_p19),
    .WD(multiplexer_7_out), .C(C), .rs1(reg_file_1_rs1), .rs2(reg_file_1_rs2), .a_0(out_1), .a_1(out_2),
    .a_2(out_3), .t_0(out_5));
  FloatREG_FILE floatreg_file_1 (
    .WE(floatRegWrite), .WD(multiplexer_7_out), .A_fs1(instr_decorder_1_p17), .A_fs2(instr_decorder_1_p18),
    .A_fd(instr_decorder_1_p19), .C(C), .fs1(floatreg_file_1_fs1), .fs2(floatreg_file_1_fs2), .fa_0(out_6),
    .Q_11(out_7), .Q_12(out_8), .Q_13(out_9));
  Extender extender_1 (.src(ImmSrc), .Imm(instr_decorder_1_p20), .Extended(extender_1_extended));
  Register #(.Bits(8)) register_1 (.D(D_pos_0), .C(C), .en(pos_0), .Q(Q_pos0));
  Register #(.Bits(8)) register_2 (.D(D_pos_1), .C(C), .en(pos_1), .Q(Q_pos1));
  Register #(.Bits(8)) register_3 (.D(D_pos_2), .C(C), .en(pos_2), .Q(Q_pos2));
  Register #(.Bits(8)) register_4 (.D(D_pos_3), .C(C), .en(pos_3), .Q(Q_pos3));
  Register #(.Bits(8)) register_5 (.D(D_onecolor_0), .C(C), .en(onecolor_0), .Q({Q_onecolor0[7], col}));
  Register #(.Bits(8)) register_6 (.D(D_onecolor_1), .C(C), .en(onecolor_1), .Q(Q_onecolor1));
  Register #(.Bits(8)) register_7 (.D(D_onecolor_2), .C(C), .en(onecolor_2), .Q(Q_onecolor2));
  Register #(.Bits(8)) register_8 (.D(D_onecolor_3), .C(C), .en(onecolor_3), .Q(Q_onecolor3));
  Register #(.Bits(8)) register_9 (.D(D_Apos_0), .C(C), .en(Apos_0), .Q(Q_Apos_0));
  Register #(.Bits(8)) register_10 (.D(D_Apos_1), .C(C), .en(Apos_0), .Q(Q_Apos_1));
  Register #(.Bits(8)) register_11 (.D(D_ASCIIptr_0), .C(C), .en(ASCIIptr_0), .Q(Q_ASCIIptr0));
  Register #(.Bits(8)) register_12 (.D(D_ASCIIptr_1), .C(C), .en(ASCIIptr_1), .Q(Q_ASCIIptr1));
  Demultiplexer #(.Selector_Bits(3)) demultiplexer_1 (
    .sel(D_exe[2:0]), .in(exe), .out_0(plotLine), .out_1(plotRect), .out_2(plotASCII));  // open: out_3, out_4, out_5, out_6, out_7
  Multiplexer #(.Bits(32)) multiplexer_3 (
    .sel(MemSrc), .in_0(reg_file_1_rs2), .in_1(floatreg_file_1_fs2), .out(multiplexer_3_out));
  Button button_2 (.out(_1P[18]));
  plotLine plotline_1 (
    .set(plotLine), .dx(dx), .dy(dy), .x_0(Q_pos0), .y_0(Q_pos1), .CC(clk), .addr(plotline_1_addr),
    .en(plotLine_en));
  plotRect plotrect_1 (
    .set(plotRect), .dx(dx), .dy(dy), .x_0(Q_pos0), .y_0(Q_pos1), .x_1(Q_pos2), .CC(clk),
    .addr(plotrect_1_addr), .en(plotRect_en));
  plotASCII plotascii_1 (
    .set(plotASCII), .x_0(Q_Apos_0), .y_0(Q_Apos_1), .ASCIIptr(Q_ASCIIptr0), .CC(clk),
    .addr(plotascii_1_addr), .en(plotASCII_en), .gen(plotASCII_gen));
  // AddressDecorder addressdecorder_1: pin names not known; wires that end beside it: ALU, multiplexer_3_out, en, addressdecorder_1_p4, {Din_3, Din_2, Din_1, Din_0}, addressdecorder_1_p6, addressdecorder_1_p7
  Button button_3 (.out(_1P[10]));
  Button button_4 (.out(_1P[8]));
  Button UP (.out(_1P[2]));
  Button LEFT (.out(_1P[3]));
  Button DOWN (.out(_1P[1]));
  Button button_5 (.out(_1P[12]));
  Button button_6 (.out(_1P[19]));
  Button button_7 (.out(_1P[17]));
  Button button_8 (.out(_1P[16]));
  Button button_9 (.out(_1P[28]));
  Multiplexer #(.Bits(32)) multiplexer_4 (
    .sel(ALUSrc), .in_0(reg_file_1_rs2), .in_1(extender_1_extended), .out(multiplexer_4_out));
  Multiplexer #(.Bits(32)) multiplexer_5 (
    .sel(FPUSrc), .in_0(floatreg_file_1_fs1), .in_1(reg_file_1_rs1), .out(multiplexer_5_out));
  Add #(.Bits(32)) add_2 (.a({{8{1'b0}}, PC[23:0]}), .b(extender_1_extended), .c_i(1'b0), .s(add_2_s));  // open: c_o
  Button RIGHT (.out(_1P[0]));
  Button button_10 (.out(_1P[13]));
  Button button_11 (.out(_1P[14]));
  Button button_12 (.out(_1P[15]));
  Button button_13 (.out(_1P[31]));
  Sub #(.Bits(9)) sub_1 (.a({1'b0, Q_pos2}), .b({1'b0, Q_pos0}), .c_i(1'b0), .s(dx));  // open: c_o
  assign driver_1_out = plotLine_en ? plotline_1_addr : 16'bz;  // Driver driver_1
  assign driver_1_out = plotRect_en ? plotrect_1_addr : 16'bz;  // Driver driver_2
  assign driver_1_out = plotASCII_en ? plotascii_1_addr : 16'bz;  // Driver driver_3
  and and_2 (b, ~funct3[0], ~funct3[1]);  // And
  and and_3 (h, funct3[0], ~funct3[1]);  // And
  and and_4 (w, ~funct3[0], funct3[1]);  // And
  // Probe on Din_0
  // Probe on Din_1
  // Probe on Din_2
  // Probe on Din_3
  and and_5 (and_5_out, addressdecorder_1_p7, MemWrite);
  ALU alu_1 (.Ctrl(ALUCtrl), .s1(reg_file_1_rs1), .s2(multiplexer_4_out), .zero(zero), .result(ALU));
  // FPU fpu_1: pin names not known; wires that end beside it: FPUCtrl, multiplexer_5_out, floatreg_file_1_fs2, fpu_1_p4
  Button button_14 (.out(_1P[26]));
  // GameControllerIO gamecontrollerio_1: pin names not known; wires that end beside it: en, _1P, {32{1'b0}}, {32{1'b0}}, {32{1'b0}}, C, addressdecorder_1_p4, gamecontrollerio_1_p8
  Byte_RAM #(.applicationType("GHDL"), .CodeFile("C:\\Users\\Gfla\\Documents\\GitHub\\RV32I\\RV32I\\Byte_RAM.vhd")) u_Byte_RAM (
    .WE(and_5_out), .C(C), .mode(funct3[1:0]), .A(addressdecorder_1_p4), .Din({Din_3, Din_2, Din_1, Din_0}),
    .A2(_2A), .D(u_Byte_RAM_d), .D2(_2D));
  Button button_15 (.out(_1P[11]));
  Button button_16 (.out(_1P[9]));
  Button button_17 (.out(_1P[6]));
  Button button_18 (.out(_1P[7]));
  Button u_B (.out(_1P[5]));
  Button button_19 (.out(_1P[20]));
  Button button_20 (.out(_1P[27]));
  Button button_21 (.out(_1P[25]));
  Button button_22 (.out(_1P[24]));
  Button button_23 (.out(_1P[29]));
  Button button_24 (.out(_1P[30]));
  or or_2 (or_2_out, b, h, w);
  or or_3 (or_3_out, h, w);
  Sub #(.Bits(9)) sub_2 (.a({1'b0, Q_pos3}), .b({1'b0, Q_pos1}), .c_i(1'b0), .s(dy));  // open: c_o
  GraphicCard #(.graphicHeight(256), .graphicWidth(256), .Bits(7)) graphiccard_1 (
    .A({1'b0, driver_1_out}), .str(str), .C(clk), .ld(1'b0), .B(1'b0), .D(col));
  Multiplexer #(.Bits(32)) multiplexer_6 (.sel(ExeSrc), .in_0(ALU), .in_1(fpu_1_p4), .out(multiplexer_6_out));
  Button A (.out(_1P[4]));
  Button button_25 (.out(_1P[21]));
  Button button_26 (.out(_1P[22]));
  Button button_27 (.out(_1P[23]));
  and and_6 (str_0, en, MemWrite, or_2_out);
  and and_7 (str_1, en, MemWrite, or_3_out);
  and and_8 (str_2, en, MemWrite, w);
  or or_4 (Q_en[0], plotLine_en, plotRect_en, plotASCII_en);
  or or_5 (str, plotLine_en, plotRect_en, plotASCII_gen);
  assign driver_4_out = en ? {D_3, D_2, D_1, D_0} : 32'bz;  // Driver driver_4
  assign driver_4_out = addressdecorder_1_p6 ? gamecontrollerio_1_p8 : 32'bz;  // Driver driver_5
  assign driver_4_out = addressdecorder_1_p7 ? u_Byte_RAM_d : 32'bz;  // Driver driver_6
  MergeData mergedata_1 (.D(driver_4_out), .funct3(funct3), .RD(mergedata_1_rd));
  // RAMViewer ramviewer_1: pin names not known; wires that end beside it: clk, _2D, _2A
  Multiplexer #(.Selector_Bits(2), .Bits(32)) multiplexer_7 (
    .sel(ResultSrc), .in_0(mergedata_1_rd), .in_1(multiplexer_6_out), .in_2(add_1_s), .in_3(add_2_s),
    .out(multiplexer_7_out));
  Multiplexer #(.Bits(32)) multiplexer_8 (
    .sel(JumpSrc), .in_0(multiplexer_6_out), .in_1(add_2_s), .out(multiplexer_8_out));
  Demultiplexer #(.Bits(8), .Selector_Bits(5)) demultiplexer_2 (
    .sel(addressdecorder_1_p4[4:0]), .in(Din_0), .out_0(D_exe), .out_2(Din_0_D_pos_0), .out_3(Din_0_D_pos_1),
    .out_4(Din_0_D_pos_2), .out_5(Din_0_D_pos_3), .out_6(Din_0_D_onecolor_0), .out_7(Din_0_D_onecolor_1),
    .out_8(Din_0_D_onecolor_2), .out_9(Din_0_D_onecolor_3), .out_10(Din_0_D_ASCIIptr_0),
    .out_11(Din_0_D_ASCIIptr_1), .out_12(Din_0_D_Apos_0), .out_13(Din_0_D_Apos_1));  // open: out_1, out_14, out_15, out_16, out_17, out_18, out_19, out_20, out_21, out_22, out_23, out_24, out_25, out_26, out_27, out_28, out_29, out_30, out_31
  Demultiplexer #(.Selector_Bits(5), .Bits(8)) demultiplexer_3 (
    .sel(addressdecorder_1_p4[4:0]), .in(Din_2), .out_0(Din_2_D_pos_0), .out_1(Din_2_D_pos_1),
    .out_2(Din_2_D_pos_2), .out_3(Din_2_D_pos_3), .out_4(Din_2_D_onecolor_0), .out_5(Din_2_D_onecolor_1),
    .out_6(Din_2_D_onecolor_2), .out_7(Din_2_D_onecolor_3), .out_8(Din_2_D_ASCIIptr_0),
    .out_9(Din_2_D_ASCIIptr_1), .out_10(Din_2_D_Apos_0), .out_11(Din_2_D_Apos_1));  // open: out_12, out_13, out_14, out_15, out_16, out_17, out_18, out_19, out_20, out_21, out_22, out_23, out_24, out_25, out_26, out_27, out_28, out_29, out_30, out_31
  Demultiplexer #(.Selector_Bits(5), .Bits(8)) demultiplexer_4 (
    .sel(addressdecorder_1_p4[4:0]), .in(Din_1), .out_1(Din_1_D_pos_0), .out_2(Din_1_D_pos_1),
    .out_3(Din_1_D_pos_2), .out_4(Din_1_D_pos_3), .out_5(Din_1_D_onecolor_0), .out_6(Din_1_D_onecolor_1),
    .out_7(Din_1_D_onecolor_2), .out_8(Din_1_D_onecolor_3), .out_9(Din_1_D_ASCIIptr_0),
    .out_10(Din_1_D_ASCIIptr_1), .out_11(Din_1_D_Apos_0), .out_12(Din_1_D_Apos_1));  // open: out_0, out_13, out_14, out_15, out_16, out_17, out_18, out_19, out_20, out_21, out_22, out_23, out_24, out_25, out_26, out_27, out_28, out_29, out_30, out_31
  Demultiplexer #(.Selector_Bits(5), .Bits(8)) demultiplexer_5 (
    .sel(addressdecorder_1_p4[4:0]), .in(Din_3), .out_0(Din_3_D_pos_1), .out_1(Din_3_D_pos_2),
    .out_2(Din_3_D_pos_3), .out_3(Din_3_D_onecolor_0), .out_4(Din_3_D_onecolor_1),
    .out_5(Din_3_D_onecolor_2), .out_6(Din_3_D_onecolor_3), .out_7(Din_3_D_ASCIIptr_0),
    .out_8(Din_3_D_ASCIIptr_1), .out_9(Din_3_D_Apos_0), .out_10(Din_3_D_Apos_1));  // open: out_11, out_12, out_13, out_14, out_15, out_16, out_17, out_18, out_19, out_20, out_21, out_22, out_23, out_24, out_25, out_26, out_27, out_28, out_29, out_30, out_31
  Demultiplexer #(.Selector_Bits(5)) demultiplexer_6 (
    .sel(addressdecorder_1_p4[4:0]), .in(str_0), .out_0(exe), .out_2(str_0_pos_0), .out_3(str_0_pos_1),
    .out_4(str_0_pos_2), .out_5(str_0_pos_3), .out_6(str_0_onecolor_0), .out_7(str_0_onecolor_1),
    .out_8(str_0_onecolor_2), .out_9(str_0_onecolor_3), .out_10(str_0_ASCIIptr_0), .out_11(str_0_ASCIIptr_1),
    .out_12(str_0_Apos_0), .out_13(str_0_Apos_1));  // open: out_1, out_14, out_15, out_16, out_17, out_18, out_19, out_20, out_21, out_22, out_23, out_24, out_25, out_26, out_27, out_28, out_29, out_30, out_31
  Demultiplexer #(.Selector_Bits(5)) demultiplexer_7 (
    .sel(addressdecorder_1_p4[4:0]), .in(str_2), .out_0(str_2_pos_0), .out_1(str_2_pos_1),
    .out_2(str_2_pos_2), .out_3(str_2_pos_3), .out_4(str_2_onecolor_0), .out_5(str_2_onecolor_1),
    .out_6(str_2_onecolor_2), .out_7(str_2_onecolor_3), .out_8(str_2_ASCIIptr_0), .out_9(str_2_ASCIIptr_1),
    .out_10(str_2_Apos_0), .out_11(str_2_Apos_1));  // open: out_12, out_13, out_14, out_15, out_16, out_17, out_18, out_19, out_20, out_21, out_22, out_23, out_24, out_25, out_26, out_27, out_28, out_29, out_30, out_31
  Demultiplexer #(.Selector_Bits(5)) demultiplexer_8 (
    .sel(addressdecorder_1_p4[4:0]), .in(str_1), .out_1(str_1_pos_0), .out_2(str_1_pos_1),
    .out_3(str_1_pos_2), .out_4(str_1_pos_3), .out_5(str_1_onecolor_0), .out_6(str_1_onecolor_1),
    .out_7(str_1_onecolor_2), .out_8(str_1_onecolor_3), .out_9(str_1_ASCIIptr_0), .out_10(str_1_ASCIIptr_1),
    .out_11(str_1_Apos_0), .out_12(str_1_Apos_1));  // open: out_0, out_13, out_14, out_15, out_16, out_17, out_18, out_19, out_20, out_21, out_22, out_23, out_24, out_25, out_26, out_27, out_28, out_29, out_30, out_31
  Demultiplexer #(.Selector_Bits(5)) demultiplexer_9 (
    .sel(addressdecorder_1_p4[4:0]), .in(str_2), .out_0(str_3_pos_1), .out_1(str_3_pos_2),
    .out_2(str_3_pos_3), .out_3(str_3_onecolor_0), .out_4(str_3_onecolor_1), .out_5(str_3_onecolor_2),
    .out_6(str_3_onecolor_3), .out_7(str_3_ASCIIptr_0), .out_8(str_3_ASCIIptr_1), .out_9(str_3_Apos_0),
    .out_10(str_3_Apos_1));  // open: out_11, out_12, out_13, out_14, out_15, out_16, out_17, out_18, out_19, out_20, out_21, out_22, out_23, out_24, out_25, out_26, out_27, out_28, out_29, out_30, out_31
  Multiplexer #(.Selector_Bits(5), .Bits(8)) multiplexer_9 (
    .sel(addressdecorder_1_p4[4:0]), .in_0({{5{1'b0}}, D_exe[2:0]}), .in_1({{7{1'b0}}, Q_en[0]}),
    .in_2(Q_pos0), .in_3(Q_pos1), .in_4(Q_pos2), .in_5(Q_pos3), .in_6({Q_onecolor0[7], col}),
    .in_7(Q_onecolor1), .in_8(Q_onecolor2), .in_9(Q_onecolor3), .in_10(Q_ASCIIptr0), .in_11(Q_ASCIIptr1),
    .in_12(Q_Apos_0), .in_13(Q_Apos_1), .in_14({8{1'b0}}), .in_15({8{1'b0}}), .in_16({8{1'b0}}),
    .in_17({8{1'b0}}), .in_18({8{1'b0}}), .in_19({8{1'b0}}), .in_20({8{1'b0}}), .in_21({8{1'b0}}),
    .in_22({8{1'b0}}), .in_23({8{1'b0}}), .in_24({8{1'b0}}), .in_25({8{1'b0}}), .in_26({8{1'b0}}),
    .in_27({8{1'b0}}), .in_28({8{1'b0}}), .in_29({8{1'b0}}), .in_30({8{1'b0}}), .in_31({8{1'b0}}), .out(D_0));
  Multiplexer #(.Selector_Bits(5), .Bits(8)) multiplexer_10 (
    .sel(addressdecorder_1_p4[4:0]), .in_0(Q_pos0), .in_1(Q_pos1), .in_2(Q_pos2), .in_3(Q_pos3),
    .in_4({Q_onecolor0[7], col}), .in_5(Q_onecolor1), .in_6(Q_onecolor2), .in_7(Q_onecolor3),
    .in_8(Q_ASCIIptr0), .in_9(Q_ASCIIptr1), .in_10(Q_Apos_0), .in_11(Q_Apos_1), .in_12({8{1'b0}}),
    .in_13({8{1'b0}}), .in_14({8{1'b0}}), .in_15({8{1'b0}}), .in_16({8{1'b0}}), .in_17({8{1'b0}}),
    .in_18({8{1'b0}}), .in_19({8{1'b0}}), .in_20({8{1'b0}}), .in_21({8{1'b0}}), .in_22({8{1'b0}}),
    .in_23({8{1'b0}}), .in_24({8{1'b0}}), .in_25({8{1'b0}}), .in_26({8{1'b0}}), .in_27({8{1'b0}}),
    .in_28({8{1'b0}}), .in_29({8{1'b0}}), .in_30({8{1'b0}}), .in_31({8{1'b0}}), .out(D_2));
  Multiplexer #(.Selector_Bits(5), .Bits(8)) multiplexer_11 (
    .sel(addressdecorder_1_p4[4:0]), .in_0({{7{1'b0}}, Q_en[0]}), .in_1(Q_pos0), .in_2(Q_pos1),
    .in_3(Q_pos2), .in_4(Q_pos3), .in_5({Q_onecolor0[7], col}), .in_6(Q_onecolor1), .in_7(Q_onecolor2),
    .in_8(Q_onecolor3), .in_9(Q_ASCIIptr0), .in_10(Q_ASCIIptr1), .in_11(Q_Apos_0), .in_12(Q_Apos_1),
    .in_13({8{1'b0}}), .in_14({8{1'b0}}), .in_15({8{1'b0}}), .in_16({8{1'b0}}), .in_17({8{1'b0}}),
    .in_18({8{1'b0}}), .in_19({8{1'b0}}), .in_20({8{1'b0}}), .in_21({8{1'b0}}), .in_22({8{1'b0}}),
    .in_23({8{1'b0}}), .in_24({8{1'b0}}), .in_25({8{1'b0}}), .in_26({8{1'b0}}), .in_27({8{1'b0}}),
    .in_28({8{1'b0}}), .in_29({8{1'b0}}), .in_30({8{1'b0}}), .in_31({8{1'b0}}), .out(D_1));
  Multiplexer #(.Selector_Bits(5), .Bits(8)) multiplexer_12 (
    .sel(addressdecorder_1_p4[4:0]), .in_0(Q_pos1), .in_1(Q_pos2), .in_2(Q_pos3),
    .in_3({Q_onecolor0[7], col}), .in_4(Q_onecolor1), .in_5(Q_onecolor2), .in_6(Q_onecolor3),
    .in_7(Q_ASCIIptr0), .in_8(Q_ASCIIptr1), .in_9(Q_Apos_0), .in_10(Q_Apos_1), .in_11({8{1'b0}}),
    .in_12({8{1'b0}}), .in_13({8{1'b0}}), .in_14({8{1'b0}}), .in_15({8{1'b0}}), .in_16({8{1'b0}}),
    .in_17({8{1'b0}}), .in_18({8{1'b0}}), .in_19({8{1'b0}}), .in_20({8{1'b0}}), .in_21({8{1'b0}}),
    .in_22({8{1'b0}}), .in_23({8{1'b0}}), .in_24({8{1'b0}}), .in_25({8{1'b0}}), .in_26({8{1'b0}}),
    .in_27({8{1'b0}}), .in_28({8{1'b0}}), .in_29({8{1'b0}}), .in_30({8{1'b0}}), .in_31({8{1'b0}}), .out(D_3));

  assign PC[31:24] = {8{1'b0}};

  // Other names for the same wires on the sheet: a_0[31:0] = out_1; A_1 = _1P[4]; a_4[31:0] = out_2; B_1 = _1P[5];
  //   CC = clk; Q_exe[2:0] = D_exe[2:0]; DOWN_1 = _1P[1]; fa_0[31:0] = out_6; L1_1 = _1P[8]; L2_1 = _1P[10];
  //   L3_1 = _1P[28]; LE_1 = _1P[14]; LEFT_1 = _1P[3]; LN_1 = _1P[12]; LNE_1 = _1P[13]; LNW_1 = _1P[19];
  //   LS_1 = _1P[16]; LSE_1 = _1P[15]; LSW_1 = _1P[17]; LW_1 = _1P[18]; Q_11[31:0] = out_7; Q_12[31:0] = out_8;
  //   Q_13[31:0] = out_9; Q_onecolor0[6:0] = col; R1_1 = _1P[9]; R2_1 = _1P[11]; R3_1 = _1P[29]; RE_1 = _1P[22];
  //   RIGHT_1 = _1P[0]; RN_1 = _1P[20]; RNE_1 = _1P[21]; RNW_1 = _1P[27]; RS_1 = _1P[24]; RSE_1 = _1P[23];
  //   RSW_1 = _1P[25]; RW_1 = _1P[26]; SELECT_1 = _1P[31]; START_1 = _1P[30]; t_0[31:0] = out_5; t_2[31:0] = out_3;
  //   UP_1 = _1P[2]; WE = MemWrite; X_1 = _1P[6]; Y_1 = _1P[7]

  // Notes on the sheet:
  //   clk: Hz: 50000
  //   rom_1 loads out.hex
  //   x_0
  //   y_0
  //   x_1
  //   y_1
endmodule
