// Digital circuit uint2float.dig as structural Verilog
module uint2float (
  input  [31:0] L,
  output [31:0] uf
);

  wire and_1_out, or_1_out, or_2_out, priorityencoder_1_any;
  wire [4:0] priorityencoder_1_num;
  wire [7:0] add_2_s;
  wire [22:0] add_1_s;
  wire [63:0] barrelshifter_1_out;

  PriorityEncoder #(.Selector_Bits(5)) priorityencoder_1 (
    .in0(L[0]), .in1(L[1]), .in2(L[2]), .in3(L[3]), .in4(L[4]), .in5(L[5]), .in6(L[6]), .in7(L[7]),
    .in8(L[8]), .in9(L[9]), .in10(L[10]), .in11(L[11]), .in12(L[12]), .in13(L[13]), .in14(L[14]),
    .in15(L[15]), .in16(L[16]), .in17(L[17]), .in18(L[18]), .in19(L[19]), .in20(L[20]), .in21(L[21]),
    .in22(L[22]), .in23(L[23]), .in24(L[24]), .in25(L[25]), .in26(L[26]), .in27(L[27]), .in28(L[28]),
    .in29(L[29]), .in30(L[30]), .in31(L[31]), .num(priorityencoder_1_num), .any(priorityencoder_1_any));
  BarrelShifter #(.Bits(64), .direction("right")) barrelshifter_1 (
    .in({L, {32{1'b0}}}), .shift({2'b00, priorityencoder_1_num}), .out(barrelshifter_1_out));
  or or_1 (or_1_out, barrelshifter_1_out[6], barrelshifter_1_out[5], barrelshifter_1_out[4], barrelshifter_1_out[3], barrelshifter_1_out[2], barrelshifter_1_out[1], barrelshifter_1_out[0]);
  or or_2 (or_2_out, or_1_out, barrelshifter_1_out[7], barrelshifter_1_out[9]);
  and and_1 (and_1_out, or_2_out, barrelshifter_1_out[8]);
  Add #(.Bits(23)) add_1 (.a(barrelshifter_1_out[31:9]), .b({23{1'b0}}), .c_i(1'b1), .s(add_1_s));  // open: c_o
  Add #(.Bits(8)) add_2 (.a({3'b000, priorityencoder_1_num}), .b(8'h7f), .c_i(1'b0), .s(add_2_s));  // open: c_o
  Multiplexer #(.Bits(23)) multiplexer_1 (
    .sel(and_1_out), .in_0(barrelshifter_1_out[31:9]), .in_1(add_1_s), .out(uf[22:0]));
  Multiplexer #(.Bits(8)) multiplexer_2 (
    .sel(priorityencoder_1_any), .in_0({8{1'b0}}), .in_1(add_2_s), .out(uf[30:23]));

  assign uf[31] = 1'b0;
endmodule
